// Logisim project D_flip_flop.circ as structural Verilog
module R_S_latch (
  input  R,
  input  S,
  output Q,
  output Qbar
);

  nor nor_1 (Q, R, Qbar);
  nor nor_2 (Qbar, Q, S);
endmodule

module D_latch (
  input  WE,
  input  D,
  output Q,
  output Qbar
);

  wire and_1_out, and_2_out, not_1_out;

  not not_1 (not_1_out, D);
  and and_1 (and_1_out, not_1_out, WE);
  and and_2 (and_2_out, WE, D);
  R_S_latch r_s_latch_1 (.R(and_1_out), .S(and_2_out), .Q(Q), .Qbar(Qbar));
endmodule

module D_ff (
  input  CLK,
  input  D,
  output Q,
  output Qbar
);

  wire d_latch_1_q, not_1_out;

  not not_1 (not_1_out, CLK);
  D_latch d_latch_1 (.WE(not_1_out), .D(D), .Q(d_latch_1_q));  // open: Qbar
  D_latch d_latch_2 (.WE(CLK), .D(d_latch_1_q), .Q(Q), .Qbar(Qbar));
endmodule

module reg1 (
  input  CLK,
  input  D,
  input  EN,
  output Q
);

  wire multiplexer_1_out;

  Multiplexer multiplexer_1 (.in0(Q), .in1(D), .out(multiplexer_1_out), .sel(EN));
  D_ff d_ff_1 (.CLK(CLK), .D(multiplexer_1_out), .Q(Q));  // open: Qbar
endmodule

module reg4 (
  input  CLK,
  input  EN,
  input  D3,
  input  D2,
  input  D1,
  input  D0,
  output Q3,
  output Q2,
  output Q1,
  output Q0
);

  reg1 reg1_1 (.CLK(CLK), .D(D3), .EN(EN), .Q(Q3));
  reg1 reg1_2 (.CLK(CLK), .D(D2), .EN(EN), .Q(Q2));
  reg1 reg1_3 (.CLK(CLK), .D(D1), .EN(EN), .Q(Q1));
  reg1 reg1_4 (.CLK(CLK), .D(D0), .EN(EN), .Q(Q0));
endmodule
