// Logisim project COMS_Gate - 副本.circ as structural Verilog
module COMS_NOT_Gate (
  input  A,
  output Y
);

  Transistor transistor_1 (.in(1'b1), .out(Y), .gate(A));
  Transistor #(.\type ("n")) transistor_2 (.in(1'b0), .out(Y), .gate(A));
endmodule

module CMOS_NAND_Gate (
  input  A,
  input  B,
  output Y
);

  wire transistor_3_out;

  Transistor transistor_1 (.in(1'b1), .out(Y), .gate(B));
  Transistor #(.\type ("n")) transistor_2 (.in(transistor_3_out), .out(Y), .gate(A));
  Transistor #(.\type ("n")) transistor_3 (.in(1'b0), .out(transistor_3_out), .gate(B));
  Transistor transistor_4 (.in(1'b1), .out(Y), .gate(A));
endmodule

module CMOS_NAD_Gate (
  input  A,
  input  B,
  output Y
);

  wire transistor_3_out, transistor_5_out;

  Transistor transistor_1 (.in(1'b1), .out(Y), .gate(transistor_3_out));
  Transistor #(.\type ("n")) transistor_2 (.in(1'b0), .out(Y), .gate(transistor_3_out));
  Transistor transistor_3 (.in(1'b1), .out(transistor_3_out), .gate(B));
  Transistor #(.\type ("n")) transistor_4 (.in(transistor_5_out), .out(transistor_3_out), .gate(A));
  Transistor #(.\type ("n")) transistor_5 (.in(1'b0), .out(transistor_5_out), .gate(B));
  Transistor transistor_6 (.in(1'b1), .out(transistor_3_out), .gate(A));
endmodule

module CMOS_NOR_Gate (
  input  A,
  input  B,
  output Y
);

  wire transistor_3_out;

  Transistor #(.\type ("n")) transistor_1 (.in(1'b0), .out(Y), .gate(B));
  Transistor transistor_2 (.in(transistor_3_out), .out(Y), .gate(A));
  Transistor transistor_3 (.in(1'b1), .out(transistor_3_out), .gate(B));
  Transistor #(.\type ("n")) transistor_4 (.in(1'b0), .out(Y), .gate(A));
endmodule

module CMOS_OR_Gate (
  input  A,
  input  B,
  output Y
);

  wire transistor_3_out, transistor_5_out;

  Transistor transistor_1 (.in(1'b1), .out(Y), .gate(transistor_3_out));
  Transistor #(.\type ("n")) transistor_2 (.in(1'b0), .out(Y), .gate(transistor_3_out));
  Transistor #(.\type ("n")) transistor_3 (.in(1'b0), .out(transistor_3_out), .gate(B));
  Transistor transistor_4 (.in(transistor_5_out), .out(transistor_3_out), .gate(A));
  Transistor transistor_5 (.in(1'b1), .out(transistor_5_out), .gate(B));
  Transistor #(.\type ("n")) transistor_6 (.in(1'b0), .out(transistor_3_out), .gate(A));
endmodule

module CMOS_XOR_Gate (
  input  A,
  input  B,
  output Y
);

  wire transmission_1_p3;

  Transistor transistor_1 (.in(A), .out(Y), .gate(B));
  // Transmission_Gate transmission_1: pin names not known; wires that end beside it: B, A, transmission_1_p3, Y
  Transistor #(.\type ("n")) transistor_2 (.in(transmission_1_p3), .out(Y), .gate(B));
  Transistor transistor_3 (.in(1'b1), .out(transmission_1_p3), .gate(A));
  Transistor #(.\type ("n")) transistor_4 (.in(1'b0), .out(transmission_1_p3), .gate(A));
endmodule

module CMOS_XNOR_Gate (
  input  A,
  input  B,
  output C
);

  wire transmission_1_p3, transmission_1_p4;

  Transistor transistor_1 (.in(1'b1), .out(C), .gate(transmission_1_p4));
  Transistor #(.\type ("n")) transistor_2 (.in(1'b0), .out(C), .gate(transmission_1_p4));
  // Transmission_Gate transmission_1: pin names not known; wires that end beside it: B, A, transmission_1_p3, transmission_1_p4
  Transistor transistor_3 (.in(A), .out(transmission_1_p4), .gate(B));
  Transistor #(.\type ("n")) transistor_4 (.in(transmission_1_p3), .out(transmission_1_p4), .gate(B));
  Transistor transistor_5 (.in(1'b1), .out(transmission_1_p3), .gate(A));
  Transistor #(.\type ("n")) transistor_6 (.in(1'b0), .out(transmission_1_p3), .gate(A));
endmodule
