// Logisim project full-subtractor.circ as structural Verilog
module half_Subtractor (
  input  A,
  input  B,
  output Diff,
  output Borrow
);

  wire not_1_out;

  not not_1 (not_1_out, A);
  xor xor_1 (Diff, A, B);
  and and_1 (Borrow, B, not_1_out);
endmodule

module full_Subtractor (
  input  A,
  input  B,
  input  Bin,
  output Diff,
  output Bout
);

  wire and_1_out, and_2_out, not_1_out, not_2_out, xor_1_out;

  not not_1 (not_1_out, A);
  xor xor_1 (xor_1_out, A, B);
  not not_2 (not_2_out, xor_1_out);
  and and_1 (and_1_out, B, not_1_out);
  xor xor_2 (Diff, xor_1_out, Bin);
  and and_2 (and_2_out, Bin, not_2_out);
  or or_1 (Bout, and_2_out, and_1_out);
endmodule

module full_Subtractor_by_half (
  input  A,
  input  B,
  input  Bin,
  output Diff,
  output Bout
);

  wire half_subtractor_1_borrow, half_subtractor_1_diff, half_subtractor_2_borrow;

  half_Subtractor half_subtractor_1 (.A(A), .B(B), .Diff(half_subtractor_1_diff), .Borrow(half_subtractor_1_borrow));
  half_Subtractor half_subtractor_2 (
    .A(half_subtractor_1_diff), .B(Bin), .Diff(Diff), .Borrow(half_subtractor_2_borrow));
  or or_1 (Bout, half_subtractor_1_borrow, half_subtractor_2_borrow);
endmodule

module full_Subtractor_4 (
  input  A3,
  input  A2,
  input  A1,
  input  A0,
  input  B3,
  input  B2,
  input  B1,
  input  B0,
  input  Bin,
  output D3,
  output D2,
  output D1,
  output D0,
  output Bout
);

  wire full_subtractor_1_bout, full_subtractor_2_bout, full_subtractor_3_bout;

  full_Subtractor full_subtractor_1 (.A(A0), .B(B0), .Bin(Bin), .Diff(D0), .Bout(full_subtractor_1_bout));
  full_Subtractor full_subtractor_2 (
    .A(A1), .B(B1), .Bin(full_subtractor_1_bout), .Diff(D1), .Bout(full_subtractor_2_bout));
  full_Subtractor full_subtractor_3 (
    .A(A2), .B(B2), .Bin(full_subtractor_2_bout), .Diff(D2), .Bout(full_subtractor_3_bout));
  full_Subtractor full_subtractor_4 (.A(A3), .B(B3), .Bin(full_subtractor_3_bout), .Diff(D3), .Bout(Bout));
endmodule
