// Logisim project half-adder.circ as structural Verilog: 1 circuit, main circuit main
module main (
  input  A,
  input  B
);

  wire AND1_out, XOR1_out;

  and AND1 (AND1_out, A, B);
  LED Carry (.in(AND1_out));
  xor XOR1 (XOR1_out, B, A);
  LED Sum (.in(XOR1_out));
endmodule
