// Logisim project f5-scpu.circ as structural Verilog
module sCPU (
  input  CLK,
  input  RUN,
  input  CLR
);

  wire and_1_out, and_2_out, and_3_out, and_4_out, equal8_1_e, multiplexer_1_out, multiplexer_2_out,
       multiplexer_4_out, multiplexer_5_out, not_1_out, not_2_out, not_3_out, or_1_out, or_2_out;
  wire [1:0] rom_1_data;
  wire [3:0] adder4_1_s0, multiplexer_3_out, reg4_1_q0, rom_1_data_3;
  wire [7:0] adder8_1_s0, gpr4x8_1_r0, gpr4x8_1_r1, gpr4x8_1_r2, gpr4x8_1_r3, gpr4x8_1_rdata1,
       gpr4x8_1_rdata2, multiplexer_6_out;
  wire [7:6] rom_1_data_2;

  or or_1 (or_1_out, RUN, CLR);
  reg4 reg4_1 (
    .CLK(CLK), .EN(or_1_out), .D3(multiplexer_1_out), .D2(multiplexer_2_out), .D1(multiplexer_4_out),
    .D0(multiplexer_5_out), .Q3(reg4_1_q0[3]), .Q2(reg4_1_q0[2]), .Q1(reg4_1_q0[1]), .Q0(reg4_1_q0[0]));
  // Probe on reg4_1_q0
  ROM #(.addrWidth(4)) rom_1 (.addr(reg4_1_q0), .data({rom_1_data_2, rom_1_data, rom_1_data_3}));
  adder4 adder4_1 (
    .A3(reg4_1_q0[3]), .A2(reg4_1_q0[2]), .A1(reg4_1_q0[1]), .A0(reg4_1_q0[0]), .B3(1'b0), .B2(1'b0),
    .B1(1'b0), .B0(1'b1), .Cin(1'b0), .S3(adder4_1_s0[3]), .S2(adder4_1_s0[2]), .S1(adder4_1_s0[1]),
    .S0(adder4_1_s0[0]));  // open: Cout
  Multiplexer multiplexer_1 (.in0(multiplexer_3_out[3]), .in1(1'b0), .out(multiplexer_1_out), .sel(CLR));
  Multiplexer multiplexer_2 (.in0(multiplexer_3_out[2]), .in1(1'b0), .out(multiplexer_2_out), .sel(CLR));
  Multiplexer #(.width(4)) multiplexer_3 (
    .in0(adder4_1_s0), .in1({rom_1_data, rom_1_data_3[3:2]}), .out(multiplexer_3_out), .sel(and_1_out));
  Multiplexer multiplexer_4 (.in0(multiplexer_3_out[1]), .in1(1'b0), .out(multiplexer_4_out), .sel(CLR));
  and and_1 (and_1_out, and_2_out, not_3_out);
  // Probe on {rom_1_data_2, rom_1_data, rom_1_data_3}
  Multiplexer multiplexer_5 (.in0(multiplexer_3_out[0]), .in1(1'b0), .out(multiplexer_5_out), .sel(CLR));
  and and_2 (and_2_out, rom_1_data_2[6], rom_1_data_2[7]);
  not not_1 (not_1_out, rom_1_data_2[6]);
  not not_2 (not_2_out, rom_1_data_2[7]);
  and and_3 (and_3_out, not_2_out, not_1_out);
  and and_4 (and_4_out, rom_1_data_2[7], not_1_out);
  or or_2 (or_2_out, and_4_out, and_3_out);
  Multiplexer #(.width(8)) multiplexer_6 (
    .in0({4'b0000, rom_1_data_3}), .in1(adder8_1_s0), .out(multiplexer_6_out), .sel(and_3_out));
  gpr4x8 gpr4x8_1 (
    .CLK(CLK), .wen(or_2_out), .waddr(rom_1_data), .wdata(multiplexer_6_out), .raddr1(rom_1_data_3[3:2]),
    .raddr2(rom_1_data_3[1:0]), .r3(gpr4x8_1_r3), .r2(gpr4x8_1_r2), .r1(gpr4x8_1_r1), .r0(gpr4x8_1_r0),
    .rdata1(gpr4x8_1_rdata1), .rdata2(gpr4x8_1_rdata2));
  // Probe on gpr4x8_1_r0
  // Probe on gpr4x8_1_r1
  adder8 adder8_1 (
    .B7(gpr4x8_1_rdata2[7]), .B6(gpr4x8_1_rdata2[6]), .B5(gpr4x8_1_rdata2[5]), .B4(gpr4x8_1_rdata2[4]),
    .B3(gpr4x8_1_rdata2[3]), .B2(gpr4x8_1_rdata2[2]), .B1(gpr4x8_1_rdata2[1]), .B0(gpr4x8_1_rdata2[0]),
    .A7(gpr4x8_1_rdata1[7]), .A6(gpr4x8_1_rdata1[6]), .A5(gpr4x8_1_rdata1[5]), .A4(gpr4x8_1_rdata1[4]),
    .A3(gpr4x8_1_rdata1[3]), .A2(gpr4x8_1_rdata1[2]), .A1(gpr4x8_1_rdata1[1]), .A0(gpr4x8_1_rdata1[0]),
    .S7(adder8_1_s0[7]), .S6(adder8_1_s0[6]), .S5(adder8_1_s0[5]), .S4(adder8_1_s0[4]), .S3(adder8_1_s0[3]),
    .S2(adder8_1_s0[2]), .S1(adder8_1_s0[1]), .S0(adder8_1_s0[0]));  // open: Cin, Cout
  // Probe on gpr4x8_1_r2
  // Probe on gpr4x8_1_r3
  equal8 equal8_1 (.A(gpr4x8_1_r0), .B(gpr4x8_1_rdata2), .E(equal8_1_e));
  not not_3 (not_3_out, equal8_1_e);

  // Notes on the sheet:
  //   contents of rom_1 (hex, n*v repeats v):
  //   8a 90 a0 b1 17 29 d1 df
endmodule

module reg8 (
  input  CLK,
  input  EN,
  input  D7,
  input  D6,
  input  D5,
  input  D4,
  input  D3,
  input  D2,
  input  D1,
  input  D0,
  output Q7,
  output Q6,
  output Q5,
  output Q4,
  output Q3,
  output Q2,
  output Q1,
  output Q0
);

  reg4 reg4_1 (.CLK(CLK), .EN(EN), .D3(D7), .D2(D6), .D1(D5), .D0(D4), .Q3(Q7), .Q2(Q6), .Q1(Q5), .Q0(Q4));
  reg4 reg4_2 (.CLK(CLK), .EN(EN), .D3(D3), .D2(D2), .D1(D1), .D0(D0), .Q3(Q3), .Q2(Q2), .Q1(Q1), .Q0(Q0));
endmodule

module gpr4x8 (
  input  CLK,
  input  wen,
  input  [1:0] waddr,
  input  [7:0] wdata,
  input  [1:0] raddr1,
  input  [1:0] raddr2,
  output [7:0] r3,
  output [7:0] r2,
  output [7:0] r1,
  output [7:0] r0,
  output [7:0] rdata1,
  output [7:0] rdata2
);

  wire decoder_1_out0, decoder_1_out1, decoder_1_out2, decoder_1_out3;

  Decoder #(.select(2)) decoder_1 (
    .out0(decoder_1_out0), .out1(decoder_1_out1), .out2(decoder_1_out2), .out3(decoder_1_out3), .sel(waddr),
    .en(wen));
  reg8 reg8_1 (
    .CLK(CLK), .EN(decoder_1_out3), .D7(wdata[7]), .D6(wdata[6]), .D5(wdata[5]), .D4(wdata[4]),
    .D3(wdata[3]), .D2(wdata[2]), .D1(wdata[1]), .D0(wdata[0]), .Q7(r3[7]), .Q6(r3[6]), .Q5(r3[5]),
    .Q4(r3[4]), .Q3(r3[3]), .Q2(r3[2]), .Q1(r3[1]), .Q0(r3[0]));
  reg8 reg8_2 (
    .CLK(CLK), .EN(decoder_1_out2), .D7(wdata[7]), .D6(wdata[6]), .D5(wdata[5]), .D4(wdata[4]),
    .D3(wdata[3]), .D2(wdata[2]), .D1(wdata[1]), .D0(wdata[0]), .Q7(r2[7]), .Q6(r2[6]), .Q5(r2[5]),
    .Q4(r2[4]), .Q3(r2[3]), .Q2(r2[2]), .Q1(r2[1]), .Q0(r2[0]));
  reg8 reg8_3 (
    .CLK(CLK), .EN(decoder_1_out1), .D7(wdata[7]), .D6(wdata[6]), .D5(wdata[5]), .D4(wdata[4]),
    .D3(wdata[3]), .D2(wdata[2]), .D1(wdata[1]), .D0(wdata[0]), .Q7(r1[7]), .Q6(r1[6]), .Q5(r1[5]),
    .Q4(r1[4]), .Q3(r1[3]), .Q2(r1[2]), .Q1(r1[1]), .Q0(r1[0]));
  reg8 reg8_4 (
    .CLK(CLK), .EN(decoder_1_out0), .D7(wdata[7]), .D6(wdata[6]), .D5(wdata[5]), .D4(wdata[4]),
    .D3(wdata[3]), .D2(wdata[2]), .D1(wdata[1]), .D0(wdata[0]), .Q7(r0[7]), .Q6(r0[6]), .Q5(r0[5]),
    .Q4(r0[4]), .Q3(r0[3]), .Q2(r0[2]), .Q1(r0[1]), .Q0(r0[0]));
  Multiplexer #(.select(2), .width(8)) multiplexer_1 (
    .in0(r0), .in1(r1), .in2(r2), .in3(r3), .out(rdata1), .sel(raddr1));
  Multiplexer #(.select(2), .width(8)) multiplexer_2 (
    .in0(r0), .in1(r1), .in2(r2), .in3(r3), .out(rdata2), .sel(raddr2));
endmodule

module adder8 (
  input  B7,
  input  B6,
  input  B5,
  input  B4,
  input  B3,
  input  B2,
  input  B1,
  input  B0,
  input  A7,
  input  A6,
  input  A5,
  input  A4,
  input  A3,
  input  A2,
  input  A1,
  input  A0,
  input  Cin,
  output Cout,
  output S7,
  output S6,
  output S5,
  output S4,
  output S3,
  output S2,
  output S1,
  output S0
);

  wire adder4_1_cout;

  adder4 adder4_1 (
    .A3(A3), .A2(A2), .A1(A1), .A0(A0), .B3(B3), .B2(B2), .B1(B1), .B0(B0), .Cin(Cin), .Cout(adder4_1_cout),
    .S3(S3), .S2(S2), .S1(S1), .S0(S0));
  adder4 adder4_2 (
    .A3(A7), .A2(A6), .A1(A5), .A0(A4), .B3(B7), .B2(B6), .B1(B5), .B0(B4), .Cin(adder4_1_cout), .Cout(Cout),
    .S3(S7), .S2(S6), .S1(S5), .S0(S4));
endmodule

module equal8 (
  input  [7:0] A,
  input  [7:0] B,
  output E
);

  wire or_1_out, xor_1_out, xor_2_out, xor_3_out, xor_4_out, xor_5_out, xor_6_out, xor_7_out, xor_8_out;

  xor xor_1 (xor_1_out, A[0], B[0]);
  xor xor_2 (xor_2_out, A[1], B[1]);
  xor xor_3 (xor_3_out, A[2], B[2]);
  xor xor_4 (xor_4_out, A[3], B[3]);
  xor xor_5 (xor_5_out, A[4], B[4]);
  xor xor_6 (xor_6_out, A[5], B[5]);
  xor xor_7 (xor_7_out, A[6], B[6]);
  xor xor_8 (xor_8_out, A[7], B[7]);
  or or_1 (or_1_out, xor_1_out, xor_2_out, xor_3_out, xor_4_out, xor_5_out, xor_6_out, xor_7_out, xor_8_out);
  not not_1 (E, or_1_out);
endmodule

module full_adder (
  input  A,
  input  B,
  input  Cin,
  output Sum,
  output Cout
);

  wire AND1_out, AND2_out, XOR1_out;

  xor XOR1 (XOR1_out, A, B);
  and AND1 (AND1_out, B, A);
  and AND2 (AND2_out, Cin, XOR1_out);
  xor XOR2 (Sum, XOR1_out, Cin);
  or OR1 (Cout, AND2_out, AND1_out);
endmodule

module adder4 (
  input  A3,
  input  A2,
  input  A1,
  input  A0,
  input  B3,
  input  B2,
  input  B1,
  input  B0,
  input  Cin,
  output Cout,
  output S3,
  output S2,
  output S1,
  output S0
);

  wire full_adder_1_cout, full_adder_2_cout, full_adder_3_cout;

  full_adder full_adder_1 (.A(A0), .B(B0), .Cin(Cin), .Sum(S0), .Cout(full_adder_1_cout));
  full_adder full_adder_2 (.A(A1), .B(B1), .Cin(full_adder_1_cout), .Sum(S1), .Cout(full_adder_2_cout));
  full_adder full_adder_3 (.A(A2), .B(B2), .Cin(full_adder_2_cout), .Sum(S2), .Cout(full_adder_3_cout));
  full_adder full_adder_4 (.A(A3), .B(B3), .Cin(full_adder_3_cout), .Sum(S3), .Cout(Cout));
endmodule
