// Logisim project f6-minirv-final.circ as structural Verilog: 2 circuits, main circuit miniRV
module miniRV (
  input  RUN,
  input  CLR
);

  wire add_out, addi_out, and_3_out, and_4_out, and_5_out, and_6_out, and_7_out, CLK_out, comparator_1_eq,
       comparator_2_eq, comparator_3_eq, comparator_4_eq, comparator_5_eq, comparator_6_eq, comparator_7_eq,
       comparator_8_eq, comparator_9_eq, comparator_10_eq, decoder_1_out0, decoder_1_out1, decoder_1_out2,
       decoder_1_out3, is_Mem_out, jalr_out, lbu_out, lui_out, lw_out, or_1_out, or_2_out, or_5_out,
       or_6_out, or_7_out, or_8_out, or_9_out, rgb_video_1_p3, sb_out, sw_out;
  wire [1:0] or_4_out;
  wire [4:0] rom_1_data_2;
  wire [6:0] rom_1_data_3;
  wire [7:0] multiplexer_9_out, rgb_video_1_p6_2;
  wire [23:8] rgb_video_1_p6;
  wire [31:0] adder_1_out, adder_2_out, and_2_out, bit_extender_1_out, bit_extender_2_out,
       bit_extender_3_out, gpr16x32_1_rdata1, multiplexer_1_out, multiplexer_2_out, multiplexer_3_out,
       multiplexer_4_out, multiplexer_5_out, multiplexer_6_out, multiplexer_7_out, multiplexer_8_out,
       ram_1_dout, register_1_q;
  wire [31:12] rom_1_data;
  wire [31:24] gpr16x32_1_rdata2;

  Clock CLK (.out(CLK_out));
  or or_1 (or_1_out, RUN, CLR);
  // RGB_Video #(.height(256), .width(256)) rgb_video_1: pin names not known; wires that end beside it: CLR, CLK_out, rgb_video_1_p3, adder_2_out[9:2], adder_2_out[17:10], {rgb_video_1_p6, rgb_video_1_p6_2}
  Multiplexer #(.width(32)) multiplexer_1 (
    .in0(multiplexer_2_out), .in1({32{1'b0}}), .out(multiplexer_1_out), .sel(CLR));
  Register #(.width(32)) register_1 (
    .D(multiplexer_1_out), .en(or_1_out), .clk(CLK_out), .Q(register_1_q));  // open: clr
  // Probe on register_1_q
  Multiplexer #(.width(32)) multiplexer_2 (.in0(adder_1_out), .in1(and_2_out), .out(multiplexer_2_out), .sel(jalr_out));
  Adder #(.width(32)) adder_1 (.a(register_1_q), .b(32'h4), .out(adder_1_out));  // open: cin, cout
  // Probe on register_1_q[19:2]
  ROM #(.addrWidth(18), .dataWidth(32)) rom_1 (
    .addr(register_1_q[19:2]), .data({rom_1_data, rom_1_data_2, rom_1_data_3}));
  // Probe on {rom_1_data, rom_1_data_2, rom_1_data_3}
  assign bit_extender_1_out = {{20{rom_1_data[31]}}, rom_1_data[31:20]};  // Bit_Extender bit_extender_1
  assign bit_extender_2_out = {{20{rom_1_data[31]}}, {rom_1_data[31:25], rom_1_data_2}};  // Bit_Extender bit_extender_2
  Comparator #(.width(3)) comparator_1 (.a(3'b000), .b(rom_1_data[14:12]), .eq(comparator_1_eq));  // open: gt, lt
  Comparator #(.width(3)) comparator_2 (.a(3'b010), .b(rom_1_data[14:12]), .eq(comparator_2_eq));  // open: gt, lt
  Comparator #(.width(3)) comparator_3 (.a(3'b100), .b(rom_1_data[14:12]), .eq(comparator_3_eq));  // open: gt, lt
  Comparator #(.width(7)) comparator_4 (.a(7'b0010011), .b(rom_1_data_3), .eq(comparator_4_eq));  // open: gt, lt
  Comparator #(.width(7)) comparator_5 (.a(7'b1100111), .b(rom_1_data_3), .eq(comparator_5_eq));  // open: gt, lt
  Comparator #(.width(7)) comparator_6 (.a(7'b0110011), .b(rom_1_data_3), .eq(comparator_6_eq));  // open: gt, lt
  Comparator #(.width(7)) comparator_7 (.a(7'b0110111), .b(rom_1_data_3), .eq(comparator_7_eq));  // open: gt, lt
  Comparator #(.width(7)) comparator_8 (.a(7'b0000011), .b(rom_1_data_3), .eq(comparator_8_eq));  // open: gt, lt
  Comparator #(.width(7)) comparator_9 (.a(7'b0100011), .b(rom_1_data_3), .eq(comparator_9_eq));  // open: gt, lt
  and addi (addi_out, comparator_4_eq, comparator_1_eq);
  and jalr (jalr_out, comparator_5_eq, comparator_1_eq);
  and add (add_out, comparator_6_eq, comparator_1_eq);
  buf lui (lui_out, comparator_7_eq);  // AND_Gate
  and lw (lw_out, comparator_8_eq, comparator_2_eq);
  and sw (sw_out, comparator_9_eq, comparator_2_eq);
  and lbu (lbu_out, comparator_8_eq, comparator_3_eq);
  and sb (sb_out, comparator_9_eq, comparator_1_eq);
  Multiplexer #(.select(2), .width(32)) multiplexer_3 (
    .in0(adder_2_out), .in1(adder_1_out), .in2({rom_1_data, {12{1'b0}}}), .in3(multiplexer_6_out),
    .out(multiplexer_3_out), .sel(or_4_out));
  or or_2 (or_2_out, addi_out, jalr_out, add_out, lui_out, lw_out, lbu_out);
  or or_3 (or_4_out[1], lui_out, lw_out, lbu_out);
  or or_4 (or_4_out[0], jalr_out, lw_out, lbu_out);
  and and_1 (rgb_video_1_p3, sw_out, comparator_10_eq);
  gpr16x32 gpr16x32_1 (
    .CLK(CLK_out), .wdata(multiplexer_3_out), .CLR(CLR), .waddr(rom_1_data_2[3:0]), .wen(or_2_out),
    .raddr1(rom_1_data[18:15]), .raddr2(rom_1_data[23:20]), .rdata1(gpr16x32_1_rdata1),
    .rdata2({gpr16x32_1_rdata2, rgb_video_1_p6, rgb_video_1_p6_2}));
  Multiplexer #(.width(32)) multiplexer_4 (
    .in0(bit_extender_1_out), .in1(bit_extender_2_out), .out(multiplexer_4_out), .sel(or_5_out));
  or or_5 (or_5_out, sw_out, sb_out);
  Multiplexer #(.width(32)) multiplexer_5 (
    .in0(multiplexer_4_out), .in1({gpr16x32_1_rdata2, rgb_video_1_p6, rgb_video_1_p6_2}),
    .out(multiplexer_5_out), .sel(add_out));
  assign and_2_out = 32'hfffffffe & adder_2_out;  // AND_Gate and_2, 32 bits wide
  Multiplexer #(.width(32)) multiplexer_6 (
    .in0(ram_1_dout), .in1(bit_extender_3_out), .out(multiplexer_6_out), .sel(lbu_out));
  Adder #(.width(32)) adder_2 (.a(gpr16x32_1_rdata1), .b(multiplexer_5_out), .out(adder_2_out));  // open: cin, cout
  Decoder #(.select(2)) decoder_1 (
    .out0(decoder_1_out0), .out1(decoder_1_out1), .out2(decoder_1_out2), .out3(decoder_1_out3),
    .sel(adder_2_out[1:0]));  // open: en
  Multiplexer #(.select(2), .width(32)) multiplexer_7 (
    .in0({{24{1'b0}}, rgb_video_1_p6_2}), .in1({{16{1'b0}}, rgb_video_1_p6_2, {8{1'b0}}}),
    .in2({{8{1'b0}}, rgb_video_1_p6_2, {16{1'b0}}}), .in3({rgb_video_1_p6_2, {24{1'b0}}}),
    .out(multiplexer_7_out), .sel(adder_2_out[1:0]));
  not is_Mem (is_Mem_out, comparator_10_eq);
  Multiplexer #(.width(32)) multiplexer_8 (
    .in0({gpr16x32_1_rdata2, rgb_video_1_p6, rgb_video_1_p6_2}), .in1(multiplexer_7_out),
    .out(multiplexer_8_out), .sel(sb_out));
  and and_3 (and_3_out, is_Mem_out, or_5_out);
  or or_6 (or_6_out, and_4_out, sw_out);
  or or_7 (or_7_out, and_5_out, sw_out);
  and and_4 (and_4_out, decoder_1_out3, sb_out);
  and and_5 (and_5_out, decoder_1_out2, sb_out);
  or or_8 (or_8_out, and_6_out, sw_out);
  and and_6 (and_6_out, decoder_1_out1, sb_out);
  and and_7 (and_7_out, decoder_1_out0, sb_out);
  RAM #(.addrWidth(18), .asyncread("true"), .byteenables("byteEnables"), .dataWidth(32), .\type ("nonvolatile")) ram_1 (
    .addr(adder_2_out[19:2]), .we(and_3_out), .oe(1'b1), .clk(CLK_out), .din(multiplexer_8_out),
    .dout(ram_1_dout), .be3(or_6_out), .be2(or_7_out), .be1(or_8_out), .be0(or_9_out));
  or or_9 (or_9_out, and_7_out, sw_out);
  Comparator #(.width(14)) comparator_10 (.a(14'h800), .b(adder_2_out[31:18]), .eq(comparator_10_eq));  // open: gt, lt
  Multiplexer #(.select(2), .width(8)) multiplexer_9 (
    .in0(ram_1_dout[7:0]), .in1(ram_1_dout[15:8]), .in2(ram_1_dout[23:16]), .in3(ram_1_dout[31:24]),
    .out(multiplexer_9_out), .sel(adder_2_out[1:0]));
  assign bit_extender_3_out = {{24{1'b0}}, multiplexer_9_out};  // Bit_Extender bit_extender_3

  // Notes on the sheet:
  //   contents of rom_1 (hex, n*v repeats v):
  //   413 93137 10113 10b7 dbc08093 80e7 fe012823 fea10923 fea12423 fe914203 fe4109a3 ff012783 f787b3
  //   f787b3 4b6b7 f0068693 fdc10113 d787b3 10000713 f12423 10593 100793 b00513 2112023 12023 12223 e12623
  //   e12823 f10a23 10b7 a8408093 80e7 2012083 2410113 8067 ff410113 112423 10b7 a7c08093 80e7 513 1800093
  //   80e7 812083 513 c10113 8067 852583 feb12823 fe812e23 3437 a0840413 ff014183 3401b3 1c183 ff114203
  //   440233 24203 4181b3 ff214203 440233 24203 4181b3 ff314203 440233 24203 4181b3 3237 a0020213 320233
  //   24203 ffc12403 420233 420233 410233 11b7 85c18193 fe312823 14800193 fe312623 fec22203 20067 1052703
  //   52683 452783 fe810113 e12423 112a23 fed12823 fef12623 13737 c0070713 fe012223 ff314203 fe4102a3
  //   fef14203 fe410223 fe412203 470233 24203 fe4105a3 ff214203 fe4102a3 fee14203 fe410223 fe412203 470233
  //   24203 fe410523 ff114203 fe4102a3 fed14203 fe410223 fe412203 470233 24203 fe4104a3 ff014203 fe4102a3
  //   fec14203 fe410223 fe412203 470233 24203 fe410423 fe812703 c52603 fee12823 fe812e23 3437 a0840413
  //   ff014183 3401b3 1c183 ff114203 440233 24203 4181b3 ff214203 440233 24203 4181b3 ff314203 440233
  //   24203 4181b3 3237 a0020213 320233 24203 ffc12403 420233 420233 410233 66800193 fe312823 28000193
  //   fe312623 fec22203 20067 c68733 10000513 fe812e23 fe912c23 fee12823 50413 ff012483 fe812423 feb14183
  //   3181b3 fe312423 fe914183 3181b3 fe912423 feb14203 420233 fe412423 fe914203 4181b3 3181b3 fe312a23
  //   fe912423 33237 b0020213 feb14183 4181b3 1c183 fe3103a3 fea14183 4181b3 1c183 fe310323 fe914183
  //   4181b3 1c183 fe3102a3 fe814183 4181b3 1c183 fe310223 ff412183 fe412203 440233 120213 fe412423
  //   feb14203 420233 fe412423 fe914203 4181b3 3237 b0820213 320233 ff812483 ffc12403 24203 420233 420233
  //   410233 11b7 86018193 fe312823 38800193 fe312623 fec22203 20067 812703 10000513 812823 e78733
  //   fe812e23 fe912c23 fee12823 50413 ff012483 fe812423 feb14183 3181b3 fe312423 fe914183 3181b3 fe912423
  //   feb14203 420233 fe412423 fe914203 4181b3 3181b3 fe312a23 fe912423 33237 b0020213 feb14183 4181b3
  //   1c183 fe3103a3 fea14183 4181b3 1c183 fe310323 fe914183 4181b3 1c183 fe3102a3 fe814183 4181b3 1c183
  //   fe310223 ff412183 fe412203 440233 120213 fe412423 feb14203 420233 fe412423 fe914203 4181b3 3237
  //   b0820213 320233 ff812483 ffc12403 24203 420233 420233 410233 11b7 86418193 fe312823 49800193
  //   fe312623 fec22203 20067 8*f787b3 d787b3 f787b3 f787b3 20000437 f40433 812783 c60633 c60633 fef12423
  //   feb14183 3181b3 fe312423 fe914183 fff78213 fe412423 feb14203 420233 fe412423 fe914203 4181b3 3237
  //   b1820213 418233 24203 420233 420233 410233 65800193 fe312823 53c00193 fe312623 fec22203 20067 912623
  //   493 40513 c12223 b12023 10b7 de008093 80e7 12583 412603 812783 148493 40040413 c585b3 fef12823
  //   fe912623 fe812e23 fe912c23 4b437 d0040413 ff014183 340233 100193 320023 fec14183 3401b3 18023 24183
  //   ff114483 940233 100493 920023 fed14483 9404b3 48023 24483 9181b3 ff214483 940233 100493 920023
  //   fee14483 9404b3 48023 24483 9181b3 ff314483 940233 100493 920023 fef14483 9404b3 48023 24483 9181b3
  //   3237 a0020213 320233 24203 ff812483 ffc12403 420233 420233 410233 65400193 fe312823 54400193
  //   fe312623 fec22203 20067 c12483 1012403 1412083 1810113 8067 10000713 fec12823 fee12623 fe812e23
  //   fe912c23 4b437 d0040413 ff014183 340233 100193 320023 fec14183 3401b3 18023 24183 ff114483 940233
  //   100493 920023 fed14483 9404b3 48023 24483 9181b3 ff214483 940233 100493 920023 fee14483 9404b3 48023
  //   24483 9181b3 ff314483 940233 100493 920023 fef14483 9404b3 48023 24483 9181b3 3237 a0020213 320233
  //   24203 ff812483 ffc12403 420233 420233 410233 74c00193 fe312823 28000193 fe312623 fec22203 20067
  //   812703 fee12823 fec12623 fe812e23 fe912c23 4b437 d0040413 ff014183 340233 100193 320023 fec14183
  //   3401b3 18023 24183 ff114483 940233 100493 920023 fed14483 9404b3 48023 24483 9181b3 ff214483 940233
  //   100493 920023 fee14483 9404b3 48023 24483 9181b3 ff314483 940233 100493 920023 fef14483 9404b3 48023
  //   24483 9181b3 3237 a0020213 320233 24203 ff812483 ffc12403 420233 420233 410233 11b7 83418193
  //   fe312823 38800193 fe312623 fec22203 20067 1412083 40637 20000537 1810113 1237 de020213 20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
endmodule

module gpr16x32 (
  input  CLK,
  input  [31:0] wdata,
  input  CLR,
  input  [3:0] waddr,
  input  wen,
  input  [3:0] raddr1,
  input  [3:0] raddr2,
  output [31:0] rdata1,
  output [31:0] rdata2
);

  wire decoder_1_out1, decoder_1_out2, decoder_1_out3, decoder_1_out4, decoder_1_out5, decoder_1_out6,
       decoder_1_out7, decoder_1_out8, decoder_1_out9, decoder_1_out10, decoder_1_out11, decoder_1_out12,
       decoder_1_out13, decoder_1_out14, decoder_1_out15;
  wire [31:0] register_1_q, register_2_q, register_3_q, register_4_q, register_5_q, register_6_q,
       register_7_q, register_8_q, register_9_q, register_10_q, register_11_q, register_12_q, register_13_q,
       register_14_q, register_15_q, register_16_q;

  Decoder #(.select(4)) decoder_1 (
    .out1(decoder_1_out1), .out2(decoder_1_out2), .out3(decoder_1_out3), .out4(decoder_1_out4),
    .out5(decoder_1_out5), .out6(decoder_1_out6), .out7(decoder_1_out7), .out8(decoder_1_out8),
    .out9(decoder_1_out9), .out10(decoder_1_out10), .out11(decoder_1_out11), .out12(decoder_1_out12),
    .out13(decoder_1_out13), .out14(decoder_1_out14), .out15(decoder_1_out15), .sel(waddr), .en(wen));  // open: out0
  Register #(.width(32)) register_1 (.D({32{1'b0}}), .en(1'b0), .clk(CLK), .Q(register_1_q), .clr(CLR));
  Register #(.width(32)) register_2 (.D(wdata), .en(decoder_1_out8), .clk(CLK), .Q(register_2_q), .clr(CLR));
  Register #(.width(32)) register_3 (.D(wdata), .en(decoder_1_out1), .clk(CLK), .Q(register_3_q), .clr(CLR));
  Register #(.width(32)) register_4 (.D(wdata), .en(decoder_1_out9), .clk(CLK), .Q(register_4_q), .clr(CLR));
  Register #(.width(32)) register_5 (.D(wdata), .en(decoder_1_out2), .clk(CLK), .Q(register_5_q), .clr(CLR));
  Register #(.width(32)) register_6 (.D(wdata), .en(decoder_1_out10), .clk(CLK), .Q(register_6_q), .clr(CLR));
  Register #(.width(32)) register_7 (.D(wdata), .en(decoder_1_out3), .clk(CLK), .Q(register_7_q), .clr(CLR));
  Register #(.width(32)) register_8 (.D(wdata), .en(decoder_1_out11), .clk(CLK), .Q(register_8_q), .clr(CLR));
  Register #(.width(32)) register_9 (.D(wdata), .en(decoder_1_out4), .clk(CLK), .Q(register_9_q), .clr(CLR));
  Register #(.width(32)) register_10 (.D(wdata), .en(decoder_1_out12), .clk(CLK), .Q(register_10_q), .clr(CLR));
  Register #(.width(32)) register_11 (.D(wdata), .en(decoder_1_out5), .clk(CLK), .Q(register_11_q), .clr(CLR));
  Register #(.width(32)) register_12 (.D(wdata), .en(decoder_1_out13), .clk(CLK), .Q(register_12_q), .clr(CLR));
  Register #(.width(32)) register_13 (.D(wdata), .en(decoder_1_out6), .clk(CLK), .Q(register_13_q), .clr(CLR));
  Register #(.width(32)) register_14 (.D(wdata), .en(decoder_1_out14), .clk(CLK), .Q(register_14_q), .clr(CLR));
  Register #(.width(32)) register_15 (.D(wdata), .en(decoder_1_out7), .clk(CLK), .Q(register_15_q), .clr(CLR));
  Register #(.width(32)) register_16 (.D(wdata), .en(decoder_1_out15), .clk(CLK), .Q(register_16_q), .clr(CLR));
  Multiplexer #(.select(4), .width(32)) multiplexer_1 (
    .in0(register_1_q), .in1(register_3_q), .in2(register_5_q), .in3(register_7_q), .in4(register_9_q),
    .in5(register_11_q), .in6(register_13_q), .in7(register_15_q), .in8(register_2_q), .in9(register_4_q),
    .in10(register_6_q), .in11(register_8_q), .in12(register_10_q), .in13(register_12_q),
    .in14(register_14_q), .in15(register_16_q), .out(rdata1), .sel(raddr1));
  Multiplexer #(.select(4), .width(32)) multiplexer_2 (
    .in0(register_1_q), .in1(register_3_q), .in2(register_5_q), .in3(register_7_q), .in4(register_9_q),
    .in5(register_11_q), .in6(register_13_q), .in7(register_15_q), .in8(register_2_q), .in9(register_4_q),
    .in10(register_6_q), .in11(register_8_q), .in12(register_10_q), .in13(register_12_q),
    .in14(register_14_q), .in15(register_16_q), .out(rdata2), .sel(raddr2));
endmodule
