// Logisim project F6_miniRV.circ as structural Verilog: 2 circuits, main circuit miniRV
module miniRV (
  input  RUN,
  input  CLR,
  input  CLK
);

  wire and_1_out, and_2_out, comparator_1_eq, comparator_2_eq, comparator_3_eq, comparator_4_eq,
       comparator_5_eq, comparator_6_eq, comparator_7_eq, or_1_out, or_2_out;
  wire [1:0] or_4_out;
  wire [4:0] rom_1_data_2;
  wire [6:0] rom_1_data_3;
  wire [31:0] adder_1_out, adder_2_out, and_3_out, bit_extender_1_out, bit_extender_2_out, gpr16x32_1_rdata1,
       gpr16x32_1_rdata2, multiplexer_1_out, multiplexer_2_out, multiplexer_3_out, multiplexer_4_out,
       multiplexer_5_out, ram_1_dout, register_1_q;
  wire [31:12] rom_1_data;

  or or_1 (or_1_out, RUN, CLR);
  Multiplexer #(.width(32)) multiplexer_1 (
    .in0(multiplexer_2_out), .in1({32{1'b0}}), .out(multiplexer_1_out), .sel(CLR));
  Register #(.width(32)) register_1 (.D(multiplexer_1_out), .en(or_1_out), .clk(CLK), .Q(register_1_q));  // open: clr
  // Probe on register_1_q
  Multiplexer #(.width(32)) multiplexer_2 (
    .in0(adder_1_out), .in1(and_3_out), .out(multiplexer_2_out), .sel(comparator_2_eq));
  Adder #(.width(32)) adder_1 (.a(register_1_q), .b(32'h4), .out(adder_1_out));  // open: cin, cout
  // Probe on register_1_q[5:2]
  ROM #(.addrWidth(4), .dataWidth(32)) rom_1 (
    .addr(register_1_q[5:2]), .data({rom_1_data, rom_1_data_2, rom_1_data_3}));
  // Probe on {rom_1_data, rom_1_data_2, rom_1_data_3}
  assign bit_extender_1_out = {{20{rom_1_data[31]}}, rom_1_data[31:20]};  // Bit_Extender bit_extender_1
  assign bit_extender_2_out = {{20{rom_1_data[31]}}, {rom_1_data[31:25], rom_1_data_2}};  // Bit_Extender bit_extender_2
  Comparator #(.width(7)) comparator_1 (.a(7'b0010011), .b(rom_1_data_3), .eq(comparator_1_eq));  // open: gt, lt
  Comparator #(.width(7)) comparator_2 (.a(7'b1100111), .b(rom_1_data_3), .eq(comparator_2_eq));  // open: gt, lt
  Comparator #(.width(7)) comparator_3 (.a(7'b0110011), .b(rom_1_data_3), .eq(comparator_3_eq));  // open: gt, lt
  Comparator #(.width(7)) comparator_4 (.a(7'b0110111), .b(rom_1_data_3), .eq(comparator_4_eq));  // open: gt, lt
  Comparator #(.width(7)) comparator_5 (.a(7'b0000011), .b(rom_1_data_3), .eq(comparator_5_eq));  // open: gt, lt
  Comparator #(.width(3)) comparator_6 (.a(3'b010), .b(rom_1_data[14:12]), .eq(comparator_6_eq));  // open: gt, lt
  Comparator #(.width(7)) comparator_7 (.a(7'b0100011), .b(rom_1_data_3), .eq(comparator_7_eq));  // open: gt, lt
  Multiplexer #(.select(2), .width(32)) multiplexer_3 (
    .in0(adder_2_out), .in1(adder_1_out), .in2({rom_1_data, {12{1'b0}}}), .in3(ram_1_dout),
    .out(multiplexer_3_out), .sel(or_4_out));
  or or_2 (or_2_out, comparator_1_eq, comparator_2_eq, comparator_3_eq, comparator_4_eq, and_1_out);
  or or_3 (or_4_out[1], comparator_4_eq, and_1_out);
  and and_1 (and_1_out, comparator_5_eq, comparator_6_eq);
  and and_2 (and_2_out, comparator_6_eq, comparator_7_eq);
  or or_4 (or_4_out[0], comparator_2_eq, and_1_out);
  Multiplexer #(.width(32)) multiplexer_4 (
    .in0(bit_extender_1_out), .in1(bit_extender_2_out), .out(multiplexer_4_out), .sel(and_2_out));
  gpr16x32 gpr16x32_1 (
    .CLK(CLK), .wdata(multiplexer_3_out), .CLR(CLR), .waddr(rom_1_data_2[3:0]), .wen(or_2_out),
    .raddr1(rom_1_data[18:15]), .raddr2(rom_1_data[23:20]), .rdata1(gpr16x32_1_rdata1),
    .rdata2(gpr16x32_1_rdata2));
  Multiplexer #(.width(32)) multiplexer_5 (
    .in0(multiplexer_4_out), .in1(gpr16x32_1_rdata2), .out(multiplexer_5_out), .sel(comparator_3_eq));
  Adder #(.width(32)) adder_2 (.a(gpr16x32_1_rdata1), .b(multiplexer_5_out), .out(adder_2_out));  // open: cin, cout
  RAM #(.addrWidth(6), .asyncread("true"), .dataWidth(32)) ram_1 (
    .addr(adder_2_out[7:2]), .we(and_2_out), .oe(1'b1), .clk(CLK), .din(gpr16x32_1_rdata2), .dout(ram_1_dout));
  assign and_3_out = adder_2_out & 32'hfffffffe;  // AND_Gate and_3, 32 bits wide

  // Notes on the sheet:
  //   contents of rom_1 (hex, n*v repeats v):
  //   6300293 502223
endmodule

module gpr16x32 (
  input  CLK,
  input  [31:0] wdata,
  input  CLR,
  input  [3:0] waddr,
  input  wen,
  input  [3:0] raddr1,
  input  [3:0] raddr2,
  output [31:0] rdata1,
  output [31:0] rdata2
);

  wire decoder_1_out1, decoder_1_out2, decoder_1_out3, decoder_1_out4, decoder_1_out5, decoder_1_out6,
       decoder_1_out7, decoder_1_out8, decoder_1_out9, decoder_1_out10, decoder_1_out11, decoder_1_out12,
       decoder_1_out13, decoder_1_out14, decoder_1_out15;
  wire [31:0] register_1_q, register_2_q, register_3_q, register_4_q, register_5_q, register_6_q,
       register_7_q, register_8_q, register_9_q, register_10_q, register_11_q, register_12_q, register_13_q,
       register_14_q, register_15_q, register_16_q;

  Decoder #(.select(4)) decoder_1 (
    .out1(decoder_1_out1), .out2(decoder_1_out2), .out3(decoder_1_out3), .out4(decoder_1_out4),
    .out5(decoder_1_out5), .out6(decoder_1_out6), .out7(decoder_1_out7), .out8(decoder_1_out8),
    .out9(decoder_1_out9), .out10(decoder_1_out10), .out11(decoder_1_out11), .out12(decoder_1_out12),
    .out13(decoder_1_out13), .out14(decoder_1_out14), .out15(decoder_1_out15), .sel(waddr), .en(wen));  // open: out0
  Register #(.width(32)) register_1 (.D({32{1'b0}}), .en(1'b0), .clk(CLK), .Q(register_1_q), .clr(CLR));
  Register #(.width(32)) register_2 (.D(wdata), .en(decoder_1_out8), .clk(CLK), .Q(register_2_q), .clr(CLR));
  Register #(.width(32)) register_3 (.D(wdata), .en(decoder_1_out1), .clk(CLK), .Q(register_3_q), .clr(CLR));
  Register #(.width(32)) register_4 (.D(wdata), .en(decoder_1_out9), .clk(CLK), .Q(register_4_q), .clr(CLR));
  Register #(.width(32)) register_5 (.D(wdata), .en(decoder_1_out2), .clk(CLK), .Q(register_5_q), .clr(CLR));
  Register #(.width(32)) register_6 (.D(wdata), .en(decoder_1_out10), .clk(CLK), .Q(register_6_q), .clr(CLR));
  Register #(.width(32)) register_7 (.D(wdata), .en(decoder_1_out3), .clk(CLK), .Q(register_7_q), .clr(CLR));
  Register #(.width(32)) register_8 (.D(wdata), .en(decoder_1_out11), .clk(CLK), .Q(register_8_q), .clr(CLR));
  Register #(.width(32)) register_9 (.D(wdata), .en(decoder_1_out4), .clk(CLK), .Q(register_9_q), .clr(CLR));
  Register #(.width(32)) register_10 (.D(wdata), .en(decoder_1_out12), .clk(CLK), .Q(register_10_q), .clr(CLR));
  Register #(.width(32)) register_11 (.D(wdata), .en(decoder_1_out5), .clk(CLK), .Q(register_11_q), .clr(CLR));
  Register #(.width(32)) register_12 (.D(wdata), .en(decoder_1_out13), .clk(CLK), .Q(register_12_q), .clr(CLR));
  Register #(.width(32)) register_13 (.D(wdata), .en(decoder_1_out6), .clk(CLK), .Q(register_13_q), .clr(CLR));
  Register #(.width(32)) register_14 (.D(wdata), .en(decoder_1_out14), .clk(CLK), .Q(register_14_q), .clr(CLR));
  Register #(.width(32)) register_15 (.D(wdata), .en(decoder_1_out7), .clk(CLK), .Q(register_15_q), .clr(CLR));
  Register #(.width(32)) register_16 (.D(wdata), .en(decoder_1_out15), .clk(CLK), .Q(register_16_q), .clr(CLR));
  Multiplexer #(.select(4), .width(32)) multiplexer_1 (
    .in0(register_1_q), .in1(register_3_q), .in2(register_5_q), .in3(register_7_q), .in4(register_9_q),
    .in5(register_11_q), .in6(register_13_q), .in7(register_15_q), .in8(register_2_q), .in9(register_4_q),
    .in10(register_6_q), .in11(register_8_q), .in12(register_10_q), .in13(register_12_q),
    .in14(register_14_q), .in15(register_16_q), .out(rdata1), .sel(raddr1));
  Multiplexer #(.select(4), .width(32)) multiplexer_2 (
    .in0(register_1_q), .in1(register_3_q), .in2(register_5_q), .in3(register_7_q), .in4(register_9_q),
    .in5(register_11_q), .in6(register_13_q), .in7(register_15_q), .in8(register_2_q), .in9(register_4_q),
    .in10(register_6_q), .in11(register_8_q), .in12(register_10_q), .in13(register_12_q),
    .in14(register_14_q), .in15(register_16_q), .out(rdata2), .sel(raddr2));
endmodule
