// Logisim project full_adder_4.circ as structural Verilog: 5 circuits, main circuit main
module main (
  input  in_1,
  input  in_2,
  input  in_3,
  input  in_4,
  input  in_5,
  input  in_6,
  input  in_7,
  input  in_8,
  input  in_9,
  input  in_10,
  output out_11,
  output out_12,
  output out_13,
  output out_14,
  output out_15,
  output out_16,
  output out_17,
  output out_18
);

  alu4 alu4_1 (
    .B3(in_7), .B2(in_8), .B1(in_9), .B0(in_10), .A3(in_3), .A2(in_4), .A1(in_5), .A0(in_6), .Op0(in_2),
    .Op1(in_1), .Cout(out_11), .S3(out_12), .S2(out_13), .S1(out_14), .S0(out_15), .Zero(out_16),
    .Negative(out_17), .Overflow(out_18));
endmodule

module full_adder (
  input  A,
  input  B,
  input  Cin,
  output Sum,
  output Cout
);

  wire AND1_out, AND2_out, XOR1_out;

  xor XOR1 (XOR1_out, A, B);
  and AND1 (AND1_out, B, A);
  and AND2 (AND2_out, Cin, XOR1_out);
  xor XOR2 (Sum, XOR1_out, Cin);
  or OR1 (Cout, AND2_out, AND1_out);
endmodule

module adder4 (
  input  A3,
  input  A2,
  input  A1,
  input  A0,
  input  B3,
  input  B2,
  input  B1,
  input  B0,
  input  Cin,
  output Cout,
  output S3,
  output S2,
  output S1,
  output S0
);

  wire full_adder_1_cout, full_adder_2_cout, full_adder_3_cout;

  full_adder full_adder_1 (.A(A0), .B(B0), .Cin(Cin), .Sum(S0), .Cout(full_adder_1_cout));
  full_adder full_adder_2 (.A(A1), .B(B1), .Cin(full_adder_1_cout), .Sum(S1), .Cout(full_adder_2_cout));
  full_adder full_adder_3 (.A(A2), .B(B2), .Cin(full_adder_2_cout), .Sum(S2), .Cout(full_adder_3_cout));
  full_adder full_adder_4 (.A(A3), .B(B3), .Cin(full_adder_3_cout), .Sum(S3), .Cout(Cout));
endmodule

module add_sub4 (
  input  A3,
  input  A2,
  input  A1,
  input  A0,
  input  B3,
  input  B2,
  input  B1,
  input  B0,
  input  Sub,
  output Cout,
  output S3,
  output S2,
  output S1,
  output S0,
  output Overflow
);

  wire not_1_out, xor_1_out, xor_2_out, xor_3_out, xor_4_out, xor_5_out, xor_6_out;

  xor xor_1 (xor_1_out, B0, Sub);
  xor xor_2 (xor_2_out, B1, Sub);
  xor xor_3 (xor_3_out, B2, Sub);
  xor xor_4 (xor_4_out, B3, Sub);
  xor xor_5 (xor_5_out, A3, xor_4_out);
  adder4 adder4_1 (
    .A3(A3), .A2(A2), .A1(A1), .A0(A0), .B3(xor_4_out), .B2(xor_3_out), .B1(xor_2_out), .B0(xor_1_out),
    .Cin(Sub), .Cout(Cout), .S3(S3), .S2(S2), .S1(S1), .S0(S0));
  not not_1 (not_1_out, xor_5_out);
  xor xor_6 (xor_6_out, S3, A3);
  and and_1 (Overflow, xor_6_out, not_1_out);
endmodule

module alu4 (
  input  B3,
  input  B2,
  input  B1,
  input  B0,
  input  A3,
  input  A2,
  input  A1,
  input  A0,
  input  Op0,
  input  Op1,
  output Cout,
  output S3,
  output S2,
  output S1,
  output S0,
  output Zero,
  output Negative,
  output Overflow
);

  wire adder4_1_s0, adder4_1_s1, adder4_1_s2, adder4_1_s3, and_1_out, and_2_out, and_3_out, and_4_out,
       not_1_out, or_1_out, or_2_out, or_3_out, or_4_out, or_5_out, xor_1_out, xor_2_out, xor_3_out,
       xor_4_out, xor_5_out, xor_6_out;

  xor xor_1 (xor_1_out, B0, Op0);
  xor xor_2 (xor_2_out, B1, Op0);
  xor xor_3 (xor_3_out, B2, Op0);
  xor xor_4 (xor_4_out, B3, Op0);
  and and_1 (and_1_out, A3, B3);
  and and_2 (and_2_out, A2, B2);
  and and_3 (and_3_out, A1, B1);
  and and_4 (and_4_out, A0, B0);
  xor xor_5 (xor_5_out, A3, xor_4_out);
  or or_1 (or_1_out, A3, B3);
  or or_2 (or_2_out, A2, B2);
  or or_3 (or_3_out, A1, B1);
  or or_4 (or_4_out, A0, B0);
  adder4 adder4_1 (
    .A3(A3), .A2(A2), .A1(A1), .A0(A0), .B3(xor_4_out), .B2(xor_3_out), .B1(xor_2_out), .B0(xor_1_out),
    .Cin(Op0), .Cout(Cout), .S3(adder4_1_s3), .S2(adder4_1_s2), .S1(adder4_1_s1), .S0(adder4_1_s0));
  not not_1 (not_1_out, xor_5_out);
  Multiplexer #(.select(2)) multiplexer_1 (
    .in0(adder4_1_s3), .in1(adder4_1_s3), .in2(and_1_out), .in3(or_1_out), .out(Negative), .sel({Op1, Op0}));
  Multiplexer #(.select(2)) multiplexer_2 (
    .in0(adder4_1_s2), .in1(adder4_1_s2), .in2(and_2_out), .in3(or_2_out), .out(S2), .sel({Op1, Op0}));
  xor xor_6 (xor_6_out, adder4_1_s3, A3);
  or or_5 (or_5_out, S0, S1, S2, Negative);
  Multiplexer #(.select(2)) multiplexer_3 (
    .in0(adder4_1_s1), .in1(adder4_1_s1), .in2(and_3_out), .in3(or_3_out), .out(S1), .sel({Op1, Op0}));
  and and_5 (Overflow, xor_6_out, not_1_out);
  not not_2 (Zero, or_5_out);
  Multiplexer #(.select(2)) multiplexer_4 (
    .in0(adder4_1_s0), .in1(adder4_1_s0), .in2(and_4_out), .in3(or_4_out), .out(S0), .sel({Op1, Op0}));

  assign S3 = Negative;
endmodule
