// Logisim project mux21.circ as structural Verilog: 1 circuit, main circuit main
module main (
  input  A,
  input  B,
  input  S
);

  wire multiplexer_1_out;

  Multiplexer multiplexer_1 (.in0(A), .in1(B), .out(multiplexer_1_out), .sel(S));
  LED LED1 (.in(multiplexer_1_out));
endmodule
