// Logisim project my_comparator.circ as structural Verilog: 3 circuits, main circuit main
module main (
  input  A3,
  input  A2,
  input  A1,
  input  A0,
  input  B3,
  input  B2,
  input  B1,
  input  B0,
  output Equal,
  output Greater,
  output Less
);

  comparator_4 comparator_4_1 (
    .A3(A3), .A2(A2), .A1(A1), .A0(A0), .B3(B3), .B2(B2), .B1(B1), .B0(B0), .Equal(Equal), .Greater(Greater),
    .Less(Less));
endmodule

module comparator_4 (
  input  A3,
  input  A2,
  input  A1,
  input  A0,
  input  B3,
  input  B2,
  input  B1,
  input  B0,
  output Equal,
  output Greater,
  output Less
);

  wire and_2_out, and_3_out, and_4_out, and_5_out, and_6_out, and_7_out, and_8_out, and_9_out, not_1_out,
       not_2_out, not_3_out, not_4_out, not_5_out, not_6_out, not_7_out, not_8_out, xnor_1_out, xnor_2_out,
       xnor_3_out, xnor_4_out;

  not not_1 (not_1_out, A3);
  not not_2 (not_2_out, A1);
  not not_3 (not_3_out, A0);
  not not_4 (not_4_out, A2);
  not not_5 (not_5_out, B3);
  not not_6 (not_6_out, B2);
  not not_7 (not_7_out, B1);
  not not_8 (not_8_out, B0);
  xnor xnor_1 (xnor_1_out, B0, A0);
  xnor xnor_2 (xnor_2_out, B1, A1);
  xnor xnor_3 (xnor_3_out, B2, A2);
  xnor xnor_4 (xnor_4_out, B3, A3);
  and and_1 (Equal, xnor_1_out, xnor_2_out, xnor_3_out, xnor_4_out);
  and and_2 (and_2_out, A3, not_5_out);
  and and_3 (and_3_out, xnor_4_out, A2, not_6_out);
  and and_4 (and_4_out, xnor_4_out, xnor_3_out, A1, not_7_out);
  and and_5 (and_5_out, xnor_4_out, xnor_3_out, xnor_2_out, A0, not_8_out);
  and and_6 (and_6_out, not_1_out, B3);
  and and_7 (and_7_out, xnor_4_out, not_4_out, B2);
  and and_8 (and_8_out, xnor_4_out, xnor_3_out, not_2_out, B1);
  and and_9 (and_9_out, xnor_4_out, xnor_3_out, xnor_2_out, not_3_out, B0);
  or or_1 (Greater, and_2_out, and_3_out, and_4_out, and_5_out);
  or or_2 (Less, and_6_out, and_7_out, and_8_out, and_9_out);
endmodule

module comparator_Equal_4 (
  input  A3,
  input  A2,
  input  A1,
  input  A0,
  input  B3,
  input  B2,
  input  B1,
  input  B0,
  output Equal
);

  wire xnor_1_out, xnor_2_out, xnor_3_out, xnor_4_out;

  xnor xnor_1 (xnor_1_out, B0, A0);
  xnor xnor_2 (xnor_2_out, B1, A1);
  xnor xnor_3 (xnor_3_out, B2, A2);
  xnor xnor_4 (xnor_4_out, B3, A3);
  and and_1 (Equal, xnor_1_out, xnor_2_out, xnor_3_out, xnor_4_out);
endmodule
