// Logisim project my_decoder.circ as structural Verilog: 6 circuits, main circuit main
module main (
  input  D3,
  input  D2,
  input  D1,
  input  D0,
  input  En,
  input  Mode
);

  wire dec_7seg_1_a, dec_7seg_1_b, dec_7seg_1_c, dec_7seg_1_d, dec_7seg_1_e, dec_7seg_1_f, dec_7seg_1_g,
       hex_7seg_1_a, hex_7seg_1_b, hex_7seg_1_c, hex_7seg_1_d, hex_7seg_1_e, hex_7seg_1_f, hex_7seg_1_g,
       mux_2_1_1_o, mux_2_1_2_o, mux_2_1_3_o, mux_2_1_4_o, mux_2_1_5_o, mux_2_1_6_o, mux_2_1_7_o;

  dec_7seg dec_7seg_1 (
    .D3(D3), .D2(D2), .D1(D1), .D0(D0), .En(En), .a(dec_7seg_1_a), .b(dec_7seg_1_b), .c(dec_7seg_1_c),
    .d(dec_7seg_1_d), .e(dec_7seg_1_e), .f(dec_7seg_1_f), .g(dec_7seg_1_g));
  hex_7seg hex_7seg_1 (
    .D3(D3), .D2(D2), .D1(D1), .D0(D0), .En(En), .a(hex_7seg_1_a), .b(hex_7seg_1_b), .c(hex_7seg_1_c),
    .d(hex_7seg_1_d), .e(hex_7seg_1_e), .f(hex_7seg_1_f), .g(hex_7seg_1_g));
  mux_2_1 mux_2_1_1 (.I1(dec_7seg_1_a), .I2(hex_7seg_1_a), .S(Mode), .O(mux_2_1_1_o));
  mux_2_1 mux_2_1_2 (.I1(dec_7seg_1_b), .I2(hex_7seg_1_b), .S(Mode), .O(mux_2_1_2_o));
  mux_2_1 mux_2_1_3 (.I1(dec_7seg_1_c), .I2(hex_7seg_1_c), .S(Mode), .O(mux_2_1_3_o));
  mux_2_1 mux_2_1_4 (.I1(dec_7seg_1_d), .I2(hex_7seg_1_d), .S(Mode), .O(mux_2_1_4_o));
  _7_Segment_Display u_7_segment_display_1 (
    .g(mux_2_1_7_o), .f(mux_2_1_6_o), .a(mux_2_1_1_o), .b(mux_2_1_2_o), .e(mux_2_1_5_o), .d(mux_2_1_4_o),
    .c(mux_2_1_3_o));  // open: dp
  mux_2_1 mux_2_1_5 (.I1(dec_7seg_1_e), .I2(hex_7seg_1_e), .S(Mode), .O(mux_2_1_5_o));
  mux_2_1 mux_2_1_6 (.I1(dec_7seg_1_f), .I2(hex_7seg_1_f), .S(Mode), .O(mux_2_1_6_o));
  mux_2_1 mux_2_1_7 (.I1(dec_7seg_1_g), .I2(hex_7seg_1_g), .S(Mode), .O(mux_2_1_7_o));
endmodule

module decoder_24 (
  input  A1,
  input  A0,
  output Y3,
  output Y2,
  output Y1,
  output Y0
);

  wire not_1_out, not_2_out;

  and and_1 (Y3, A1, A0);
  not not_1 (not_1_out, A0);
  and and_2 (Y2, not_1_out, A1);
  not not_2 (not_2_out, A1);
  and and_3 (Y1, A0, not_2_out);
  and and_4 (Y0, not_1_out, not_2_out);
endmodule

module decoder_4_16 (
  input  in_1,
  input  in_2,
  input  in_3,
  input  in_4,
  input  En
);

  wire decoder_1_out0, decoder_1_out1, decoder_1_out2, decoder_1_out3, decoder_1_out4, decoder_1_out5,
       decoder_1_out6, decoder_1_out7, decoder_1_out8, decoder_1_out9, decoder_1_out10, decoder_1_out11,
       decoder_1_out12, decoder_1_out13, decoder_1_out14, decoder_1_out15;

  Decoder #(.select(4)) decoder_1 (
    .out0(decoder_1_out0), .out1(decoder_1_out1), .out2(decoder_1_out2), .out3(decoder_1_out3),
    .out4(decoder_1_out4), .out5(decoder_1_out5), .out6(decoder_1_out6), .out7(decoder_1_out7),
    .out8(decoder_1_out8), .out9(decoder_1_out9), .out10(decoder_1_out10), .out11(decoder_1_out11),
    .out12(decoder_1_out12), .out13(decoder_1_out13), .out14(decoder_1_out14), .out15(decoder_1_out15),
    .sel({in_1, in_2, in_3, in_4}), .en(En));
  LED led_1 (.in(decoder_1_out15));
  LED led_2 (.in(decoder_1_out14));
  LED led_3 (.in(decoder_1_out13));
  LED led_4 (.in(decoder_1_out12));
  LED led_5 (.in(decoder_1_out11));
  LED led_6 (.in(decoder_1_out10));
  LED led_7 (.in(decoder_1_out9));
  LED led_8 (.in(decoder_1_out8));
  LED led_9 (.in(decoder_1_out7));
  LED led_10 (.in(decoder_1_out6));
  LED led_11 (.in(decoder_1_out5));
  LED led_12 (.in(decoder_1_out4));
  LED led_13 (.in(decoder_1_out3));
  LED led_14 (.in(decoder_1_out2));
  LED led_15 (.in(decoder_1_out1));
  LED led_16 (.in(decoder_1_out0));
endmodule

module dec_7seg (
  input  D3,
  input  D2,
  input  D1,
  input  D0,
  input  En,
  output a,
  output b,
  output c,
  output d,
  output e,
  output f,
  output g
);

  wire decoder_1_out0, decoder_1_out1, decoder_1_out2, decoder_1_out3, decoder_1_out4, decoder_1_out5,
       decoder_1_out6, decoder_1_out7, decoder_1_out8, decoder_1_out9;

  Decoder #(.select(4)) decoder_1 (
    .out0(decoder_1_out0), .out1(decoder_1_out1), .out2(decoder_1_out2), .out3(decoder_1_out3),
    .out4(decoder_1_out4), .out5(decoder_1_out5), .out6(decoder_1_out6), .out7(decoder_1_out7),
    .out8(decoder_1_out8), .out9(decoder_1_out9), .sel({D3, D2, D1, D0}), .en(En));  // open: out10, out11, out12, out13, out14, out15
  or or_1 (a, decoder_1_out0, decoder_1_out2, decoder_1_out3, decoder_1_out5, decoder_1_out6, decoder_1_out7, decoder_1_out8, decoder_1_out9);
  or or_2 (b, decoder_1_out0, decoder_1_out1, decoder_1_out2, decoder_1_out3, decoder_1_out4, decoder_1_out7, decoder_1_out8, decoder_1_out9);
  or or_3 (c, decoder_1_out0, decoder_1_out1, decoder_1_out3, decoder_1_out4, decoder_1_out5, decoder_1_out6, decoder_1_out7, decoder_1_out8, decoder_1_out9);
  or or_4 (d, decoder_1_out0, decoder_1_out2, decoder_1_out3, decoder_1_out5, decoder_1_out6, decoder_1_out8, decoder_1_out9);
  or or_5 (e, decoder_1_out0, decoder_1_out2, decoder_1_out6, decoder_1_out8);
  or or_6 (f, decoder_1_out0, decoder_1_out4, decoder_1_out5, decoder_1_out6, decoder_1_out8, decoder_1_out9);
  or or_7 (g, decoder_1_out2, decoder_1_out3, decoder_1_out4, decoder_1_out5, decoder_1_out6, decoder_1_out8, decoder_1_out9);
endmodule

module hex_7seg (
  input  D3,
  input  D2,
  input  D1,
  input  D0,
  input  En,
  output a,
  output b,
  output c,
  output d,
  output e,
  output f,
  output g
);

  wire decoder_1_out0, decoder_1_out1, decoder_1_out2, decoder_1_out3, decoder_1_out4, decoder_1_out5,
       decoder_1_out6, decoder_1_out7, decoder_1_out8, decoder_1_out9, decoder_1_out10, decoder_1_out11,
       decoder_1_out12, decoder_1_out13, decoder_1_out14, decoder_1_out15;

  Decoder #(.select(4)) decoder_1 (
    .out0(decoder_1_out0), .out1(decoder_1_out1), .out2(decoder_1_out2), .out3(decoder_1_out3),
    .out4(decoder_1_out4), .out5(decoder_1_out5), .out6(decoder_1_out6), .out7(decoder_1_out7),
    .out8(decoder_1_out8), .out9(decoder_1_out9), .out10(decoder_1_out10), .out11(decoder_1_out11),
    .out12(decoder_1_out12), .out13(decoder_1_out13), .out14(decoder_1_out14), .out15(decoder_1_out15),
    .sel({D3, D2, D1, D0}), .en(En));
  or or_1 (a, decoder_1_out0, decoder_1_out2, decoder_1_out3, decoder_1_out5, decoder_1_out6, decoder_1_out7, decoder_1_out8, decoder_1_out9, decoder_1_out10, decoder_1_out12, decoder_1_out14, decoder_1_out15);
  or or_2 (b, decoder_1_out0, decoder_1_out1, decoder_1_out2, decoder_1_out3, decoder_1_out4, decoder_1_out7, decoder_1_out8, decoder_1_out9, decoder_1_out10, decoder_1_out13);
  or or_3 (c, decoder_1_out0, decoder_1_out1, decoder_1_out3, decoder_1_out4, decoder_1_out5, decoder_1_out6, decoder_1_out7, decoder_1_out8, decoder_1_out9, decoder_1_out10, decoder_1_out11, decoder_1_out13);
  or or_4 (d, decoder_1_out0, decoder_1_out2, decoder_1_out3, decoder_1_out5, decoder_1_out6, decoder_1_out8, decoder_1_out9, decoder_1_out11, decoder_1_out12, decoder_1_out13, decoder_1_out14);
  or or_5 (e, decoder_1_out0, decoder_1_out2, decoder_1_out6, decoder_1_out8, decoder_1_out10, decoder_1_out11, decoder_1_out12, decoder_1_out13, decoder_1_out14, decoder_1_out15);
  or or_6 (f, decoder_1_out0, decoder_1_out4, decoder_1_out5, decoder_1_out6, decoder_1_out8, decoder_1_out9, decoder_1_out10, decoder_1_out11, decoder_1_out12, decoder_1_out14, decoder_1_out15);
  or or_7 (g, decoder_1_out2, decoder_1_out3, decoder_1_out4, decoder_1_out5, decoder_1_out6, decoder_1_out8, decoder_1_out9, decoder_1_out10, decoder_1_out11, decoder_1_out13, decoder_1_out14, decoder_1_out15);
endmodule

module mux_2_1 (
  input  I1,
  input  I2,
  input  S,
  output O
);

  wire and_1_out, and_2_out, not_1_out;

  not not_1 (not_1_out, S);
  and and_1 (and_1_out, S, I2);
  and and_2 (and_2_out, not_1_out, I1);
  or or_1 (O, and_1_out, and_2_out);
endmodule
