// Logisim project my_encoder.circ as structural Verilog
module Encoder_4_2 (
  input  I3,
  input  I2,
  input  I1,
  input  I0,
  output Y1,
  output Y0
);

  or or_1 (Y1, I2, I3);
  or or_2 (Y0, I1, I3);
endmodule

module priority_Encoder_4_2 (
  input  I3,
  input  I2,
  input  I1,
  input  I0,
  output Y1,
  output Y0,
  output Valid
);

  wire and_1_out, not_1_out;

  not not_1 (not_1_out, I2);
  and and_1 (and_1_out, I1, not_1_out);
  or or_1 (Y1, I2, I3);
  or or_2 (Y0, and_1_out, I3);
  or or_3 (Valid, I0, I1, I2, I3);
endmodule
