// Logisim project my_mux.circ as structural Verilog
module mux_1bit_4_1 (
  input  D3,
  input  D2,
  input  D1,
  input  D0,
  input  S1,
  input  S0,
  output Y
);

  wire and_1_out, and_2_out, and_3_out, and_4_out, not_1_out, not_2_out;

  not not_1 (not_1_out, S0);
  not not_2 (not_2_out, S1);
  and and_1 (and_1_out, not_2_out, not_1_out, D0);
  and and_2 (and_2_out, not_2_out, S0, D1);
  and and_3 (and_3_out, S1, not_1_out, D2);
  and and_4 (and_4_out, S1, S0, D3);
  or or_1 (Y, and_1_out, and_2_out, and_3_out, and_4_out);
endmodule

module mux_3bit_4_1 (
  input  S1,
  input  S0,
  input  D3_2,
  input  D2_2,
  input  D1_2,
  input  D0_2,
  input  D3_1,
  input  D2_1,
  input  D1_1,
  input  D0_1,
  input  D3_0,
  input  D2_0,
  input  D1_0,
  input  D0_0,
  output Y2,
  output Y1,
  output Y0
);

  mux_1bit_4_1 mux_1bit_4_1_1 (.D3(D3_2), .D2(D2_2), .D1(D1_2), .D0(D0_2), .S1(S1), .S0(S0), .Y(Y2));
  mux_1bit_4_1 mux_1bit_4_1_2 (.D3(D3_1), .D2(D2_1), .D1(D1_1), .D0(D0_1), .S1(S1), .S0(S0), .Y(Y1));
  mux_1bit_4_1 mux_1bit_4_1_3 (.D3(D3_0), .D2(D2_0), .D1(D1_0), .D0(D0_0), .S1(S1), .S0(S0), .Y(Y0));
endmodule
