// Logisim project digital-clock.circ as structural Verilog: 7 circuits, main circuit counter4
module counter4 (
  input  CLK,
  input  EN,
  input  CLR,
  output Q3,
  output Q2,
  output Q1,
  output Q0,
  output Cout
);

  wire adder4_1_s0, adder4_1_s1, adder4_1_s2, adder4_1_s3, multiplexer_1_out, multiplexer_2_out,
       multiplexer_3_out, multiplexer_4_out;

  reg4 reg4_1 (
    .CLK(CLK), .EN(EN), .D3(multiplexer_1_out), .D2(multiplexer_2_out), .D1(multiplexer_3_out),
    .D0(multiplexer_4_out), .Q3(Q3), .Q2(Q2), .Q1(Q1), .Q0(Q0));
  adder4 adder4_1 (
    .A3(Q3), .A2(Q2), .A1(Q1), .A0(Q0), .B3(1'b0), .B2(1'b0), .B1(1'b0), .B0(1'b1), .Cin(1'b0), .Cout(Cout),
    .S3(adder4_1_s3), .S2(adder4_1_s2), .S1(adder4_1_s1), .S0(adder4_1_s0));
  Multiplexer multiplexer_1 (.in0(adder4_1_s3), .in1(1'b0), .out(multiplexer_1_out), .sel(CLR));
  Multiplexer multiplexer_2 (.in0(adder4_1_s2), .in1(1'b0), .out(multiplexer_2_out), .sel(CLR));
  Multiplexer multiplexer_3 (.in0(adder4_1_s1), .in1(1'b0), .out(multiplexer_3_out), .sel(CLR));
  Multiplexer multiplexer_4 (.in0(adder4_1_s0), .in1(1'b0), .out(multiplexer_4_out), .sel(CLR));
endmodule

module adder8 (
  input  A7,
  input  A6,
  input  A5,
  input  A4,
  input  A3,
  input  A2,
  input  A1,
  input  A0,
  input  B7,
  input  B6,
  input  B5,
  input  B4,
  input  B3,
  input  B2,
  input  B1,
  input  B0,
  input  Cin,
  output Cout,
  output S7,
  output S6,
  output S5,
  output S4,
  output S3,
  output S2,
  output S1,
  output S0
);

  wire adder4_1_cout;

  adder4 adder4_1 (
    .A3(A3), .A2(A2), .A1(A1), .A0(A0), .B3(B3), .B2(B2), .B1(B1), .B0(B0), .Cin(Cin), .Cout(adder4_1_cout),
    .S3(S3), .S2(S2), .S1(S1), .S0(S0));
  adder4 adder4_2 (
    .A3(A7), .A2(A6), .A1(A5), .A0(A4), .B3(B7), .B2(B6), .B1(B5), .B0(B4), .Cin(adder4_1_cout), .Cout(Cout),
    .S3(S7), .S2(S6), .S1(S5), .S0(S4));
endmodule

module reg8 (
  input  CLK,
  input  EN,
  input  D7,
  input  D6,
  input  D5,
  input  D4,
  input  D3,
  input  D2,
  input  D1,
  input  D0,
  output Q7,
  output Q6,
  output Q5,
  output Q4,
  output Q3,
  output Q2,
  output Q1,
  output Q0
);

  reg4 reg4_1 (.CLK(CLK), .EN(EN), .D3(D7), .D2(D6), .D1(D5), .D0(D4), .Q3(Q7), .Q2(Q6), .Q1(Q5), .Q0(Q4));
  reg4 reg4_2 (.CLK(CLK), .EN(EN), .D3(D3), .D2(D2), .D1(D1), .D0(D0), .Q3(Q3), .Q2(Q2), .Q1(Q1), .Q0(Q0));
endmodule

module sum_counter (
  input  CLK,
  input  RUN,
  input  CLR,
  output C3,
  output C2,
  output C1,
  output C0,
  output Done,
  output S7,
  output S6,
  output S5,
  output S4,
  output S3,
  output S2,
  output S1,
  output S0
);

  wire adder4_1_s0, adder4_1_s1, adder4_1_s2, adder4_1_s3, adder8_1_s0, adder8_1_s1, adder8_1_s2,
       adder8_1_s3, adder8_1_s4, adder8_1_s5, adder8_1_s6, adder8_1_s7, and_1_out, multiplexer_1_out,
       multiplexer_2_out, multiplexer_3_out, multiplexer_4_out, multiplexer_5_out, multiplexer_6_out,
       multiplexer_7_out, multiplexer_8_out, multiplexer_9_out, multiplexer_10_out, multiplexer_11_out,
       multiplexer_12_out, not_1_out, not_2_out, not_3_out, or_1_out;

  and and_1 (and_1_out, RUN, not_2_out);
  or or_1 (or_1_out, and_1_out, CLR);
  reg4 reg4_1 (
    .CLK(CLK), .EN(or_1_out), .D3(multiplexer_1_out), .D2(multiplexer_2_out), .D1(multiplexer_5_out),
    .D0(multiplexer_7_out), .Q3(C3), .Q2(C2), .Q1(C1), .Q0(C0));
  not not_1 (not_1_out, C2);
  not not_2 (not_2_out, Done);
  reg8 reg8_1 (
    .CLK(CLK), .EN(or_1_out), .D7(multiplexer_3_out), .D6(multiplexer_4_out), .D5(multiplexer_6_out),
    .D4(multiplexer_8_out), .D3(multiplexer_9_out), .D2(multiplexer_10_out), .D1(multiplexer_11_out),
    .D0(multiplexer_12_out), .Q7(S7), .Q6(S6), .Q5(S5), .Q4(S4), .Q3(S3), .Q2(S2), .Q1(S1), .Q0(S0));
  not not_3 (not_3_out, C0);
  and and_2 (Done, C3, not_1_out, C1, not_3_out);
  adder4 adder4_1 (
    .A3(C3), .A2(C2), .A1(C1), .A0(C0), .B3(1'b0), .B2(1'b0), .B1(1'b0), .B0(1'b1), .Cin(1'b0),
    .S3(adder4_1_s3), .S2(adder4_1_s2), .S1(adder4_1_s1), .S0(adder4_1_s0));  // open: Cout
  adder8 adder8_1 (
    .A7(S7), .A6(S6), .A5(S5), .A4(S4), .A3(S3), .A2(S2), .A1(S1), .A0(S0), .B7(1'b0), .B6(1'b0), .B5(1'b0),
    .B4(1'b0), .B3(multiplexer_1_out), .B2(multiplexer_2_out), .B1(multiplexer_5_out),
    .B0(multiplexer_7_out), .S7(adder8_1_s7), .S6(adder8_1_s6), .S5(adder8_1_s5), .S4(adder8_1_s4),
    .S3(adder8_1_s3), .S2(adder8_1_s2), .S1(adder8_1_s1), .S0(adder8_1_s0));  // open: Cin, Cout
  Multiplexer multiplexer_1 (.in0(adder4_1_s3), .in1(1'b0), .out(multiplexer_1_out), .sel(CLR));
  Multiplexer multiplexer_2 (.in0(adder4_1_s2), .in1(1'b0), .out(multiplexer_2_out), .sel(CLR));
  Multiplexer multiplexer_3 (.in0(adder8_1_s7), .in1(1'b0), .out(multiplexer_3_out), .sel(CLR));
  Multiplexer multiplexer_4 (.in0(adder8_1_s6), .in1(1'b0), .out(multiplexer_4_out), .sel(CLR));
  Multiplexer multiplexer_5 (.in0(adder4_1_s1), .in1(1'b0), .out(multiplexer_5_out), .sel(CLR));
  Multiplexer multiplexer_6 (.in0(adder8_1_s5), .in1(1'b0), .out(multiplexer_6_out), .sel(CLR));
  Multiplexer multiplexer_7 (.in0(adder4_1_s0), .in1(1'b0), .out(multiplexer_7_out), .sel(CLR));
  Multiplexer multiplexer_8 (.in0(adder8_1_s4), .in1(1'b0), .out(multiplexer_8_out), .sel(CLR));
  Multiplexer multiplexer_9 (.in0(adder8_1_s3), .in1(1'b0), .out(multiplexer_9_out), .sel(CLR));
  Multiplexer multiplexer_10 (.in0(adder8_1_s2), .in1(1'b0), .out(multiplexer_10_out), .sel(CLR));
  Multiplexer multiplexer_11 (.in0(adder8_1_s1), .in1(1'b0), .out(multiplexer_11_out), .sel(CLR));
  Multiplexer multiplexer_12 (.in0(adder8_1_s0), .in1(1'b0), .out(multiplexer_12_out), .sel(CLR));
endmodule

module mod10 (
  input  CLK,
  input  EN,
  input  CLR,
  output Q3,
  output Q2,
  output Q1,
  output Q0,
  output Carry
);

  wire adder4_1_s0, adder4_1_s1, adder4_1_s2, adder4_1_s3, and_2_out, multiplexer_1_out, multiplexer_2_out,
       multiplexer_3_out, multiplexer_4_out, not_1_out, not_2_out, or_1_out, or_2_out;

  or or_1 (or_1_out, EN, CLR);
  and and_1 (Carry, EN, and_2_out);
  reg4 reg4_1 (
    .CLK(CLK), .EN(or_1_out), .D3(multiplexer_1_out), .D2(multiplexer_2_out), .D1(multiplexer_3_out),
    .D0(multiplexer_4_out), .Q3(Q3), .Q2(Q2), .Q1(Q1), .Q0(Q0));
  or or_2 (or_2_out, Carry, CLR);
  not not_1 (not_1_out, Q2);
  not not_2 (not_2_out, Q1);
  and and_2 (and_2_out, Q3, not_1_out, not_2_out, Q0);
  adder4 adder4_1 (
    .A3(Q3), .A2(Q2), .A1(Q1), .A0(Q0), .B3(1'b0), .B2(1'b0), .B1(1'b0), .B0(1'b1), .Cin(1'b0),
    .S3(adder4_1_s3), .S2(adder4_1_s2), .S1(adder4_1_s1), .S0(adder4_1_s0));  // open: Cout
  Multiplexer multiplexer_1 (.in0(adder4_1_s3), .in1(1'b0), .out(multiplexer_1_out), .sel(or_2_out));
  Multiplexer multiplexer_2 (.in0(adder4_1_s2), .in1(1'b0), .out(multiplexer_2_out), .sel(or_2_out));
  Multiplexer multiplexer_3 (.in0(adder4_1_s1), .in1(1'b0), .out(multiplexer_3_out), .sel(or_2_out));
  Multiplexer multiplexer_4 (.in0(adder4_1_s0), .in1(1'b0), .out(multiplexer_4_out), .sel(or_2_out));
endmodule

module mod6 (
  input  CLK,
  input  EN,
  input  CLR,
  output Q3,
  output Q2,
  output Q1,
  output Q0,
  output Carry
);

  wire adder4_1_s0, adder4_1_s1, adder4_1_s2, adder4_1_s3, and_2_out, multiplexer_1_out, multiplexer_2_out,
       multiplexer_3_out, multiplexer_4_out, not_1_out, not_2_out, or_1_out, or_2_out;

  or or_1 (or_1_out, EN, CLR);
  and and_1 (Carry, EN, and_2_out);
  reg4 reg4_1 (
    .CLK(CLK), .EN(or_1_out), .D3(multiplexer_1_out), .D2(multiplexer_2_out), .D1(multiplexer_3_out),
    .D0(multiplexer_4_out), .Q3(Q3), .Q2(Q2), .Q1(Q1), .Q0(Q0));
  or or_2 (or_2_out, Carry, CLR);
  not not_1 (not_1_out, Q3);
  not not_2 (not_2_out, Q1);
  and and_2 (and_2_out, not_1_out, Q2, not_2_out, Q0);
  adder4 adder4_1 (
    .A3(Q3), .A2(Q2), .A1(Q1), .A0(Q0), .B3(1'b0), .B2(1'b0), .B1(1'b0), .B0(1'b1), .Cin(1'b0),
    .S3(adder4_1_s3), .S2(adder4_1_s2), .S1(adder4_1_s1), .S0(adder4_1_s0));  // open: Cout
  Multiplexer multiplexer_1 (.in0(adder4_1_s3), .in1(1'b0), .out(multiplexer_1_out), .sel(or_2_out));
  Multiplexer multiplexer_2 (.in0(adder4_1_s2), .in1(1'b0), .out(multiplexer_2_out), .sel(or_2_out));
  Multiplexer multiplexer_3 (.in0(adder4_1_s1), .in1(1'b0), .out(multiplexer_3_out), .sel(or_2_out));
  Multiplexer multiplexer_4 (.in0(adder4_1_s0), .in1(1'b0), .out(multiplexer_4_out), .sel(or_2_out));
endmodule

module counter_clock (
  input  RUN,
  input  CLR
);

  wire CLK_out, dec_7seg_1_a, dec_7seg_1_b, dec_7seg_1_c, dec_7seg_1_d, dec_7seg_1_e, dec_7seg_1_f,
       dec_7seg_1_g, dec_7seg_2_a, dec_7seg_2_b, dec_7seg_2_c, dec_7seg_2_d, dec_7seg_2_e, dec_7seg_2_f,
       dec_7seg_2_g, dec_7seg_3_a, dec_7seg_3_b, dec_7seg_3_c, dec_7seg_3_d, dec_7seg_3_e, dec_7seg_3_f,
       dec_7seg_3_g, dec_7seg_4_a, dec_7seg_4_b, dec_7seg_4_c, dec_7seg_4_d, dec_7seg_4_e, dec_7seg_4_f,
       dec_7seg_4_g, min_ones_carry, min_ones_q0, min_ones_q1, min_ones_q2, min_ones_q3, min_tens_q0,
       min_tens_q1, min_tens_q2, min_tens_q3, sec_ones_carry, sec_ones_q0, sec_ones_q1, sec_ones_q2,
       sec_ones_q3, sec_tens_carry, sec_tens_q0, sec_tens_q1, sec_tens_q2, sec_tens_q3;

  Clock CLK (.out(CLK_out));
  mod10 sec_ones (
    .CLK(CLK_out), .EN(RUN), .CLR(CLR), .Q3(sec_ones_q3), .Q2(sec_ones_q2), .Q1(sec_ones_q1),
    .Q0(sec_ones_q0), .Carry(sec_ones_carry));
  mod6 sec_tens (
    .CLK(CLK_out), .EN(sec_ones_carry), .CLR(CLR), .Q3(sec_tens_q3), .Q2(sec_tens_q2), .Q1(sec_tens_q1),
    .Q0(sec_tens_q0), .Carry(sec_tens_carry));
  mod10 min_ones (
    .CLK(CLK_out), .EN(sec_tens_carry), .CLR(CLR), .Q3(min_ones_q3), .Q2(min_ones_q2), .Q1(min_ones_q1),
    .Q0(min_ones_q0), .Carry(min_ones_carry));
  mod6 min_tens (
    .CLK(CLK_out), .EN(min_ones_carry), .CLR(CLR), .Q3(min_tens_q3), .Q2(min_tens_q2), .Q1(min_tens_q1),
    .Q0(min_tens_q0));  // open: Carry
  dec_7seg dec_7seg_1 (
    .D3(sec_ones_q3), .D2(sec_ones_q2), .D1(sec_ones_q1), .D0(sec_ones_q0), .En(RUN), .a(dec_7seg_1_a),
    .b(dec_7seg_1_b), .c(dec_7seg_1_c), .d(dec_7seg_1_d), .e(dec_7seg_1_e), .f(dec_7seg_1_f), .g(dec_7seg_1_g));
  dec_7seg dec_7seg_2 (
    .D3(sec_tens_q3), .D2(sec_tens_q2), .D1(sec_tens_q1), .D0(sec_tens_q0), .En(RUN), .a(dec_7seg_2_a),
    .b(dec_7seg_2_b), .c(dec_7seg_2_c), .d(dec_7seg_2_d), .e(dec_7seg_2_e), .f(dec_7seg_2_f), .g(dec_7seg_2_g));
  dec_7seg dec_7seg_3 (
    .D3(min_ones_q3), .D2(min_ones_q2), .D1(min_ones_q1), .D0(min_ones_q0), .En(RUN), .a(dec_7seg_3_a),
    .b(dec_7seg_3_b), .c(dec_7seg_3_c), .d(dec_7seg_3_d), .e(dec_7seg_3_e), .f(dec_7seg_3_f), .g(dec_7seg_3_g));
  dec_7seg dec_7seg_4 (
    .D3(min_tens_q3), .D2(min_tens_q2), .D1(min_tens_q1), .D0(min_tens_q0), .En(RUN), .a(dec_7seg_4_a),
    .b(dec_7seg_4_b), .c(dec_7seg_4_c), .d(dec_7seg_4_d), .e(dec_7seg_4_e), .f(dec_7seg_4_f), .g(dec_7seg_4_g));
  _7_Segment_Display u_7_segment_display_1 (
    .g(dec_7seg_3_g), .f(dec_7seg_3_f), .a(dec_7seg_3_a), .b(dec_7seg_3_b), .e(dec_7seg_3_e),
    .d(dec_7seg_3_d), .c(dec_7seg_3_c));  // open: dp
  _7_Segment_Display u_7_segment_display_2 (
    .g(dec_7seg_4_g), .f(dec_7seg_4_f), .a(dec_7seg_4_a), .b(dec_7seg_4_b), .e(dec_7seg_4_e),
    .d(dec_7seg_4_d), .c(dec_7seg_4_c));  // open: dp
  _7_Segment_Display u_7_segment_display_3 (
    .g(dec_7seg_2_g), .f(dec_7seg_2_f), .a(dec_7seg_2_a), .b(dec_7seg_2_b), .e(dec_7seg_2_e),
    .d(dec_7seg_2_d), .c(dec_7seg_2_c));  // open: dp
  _7_Segment_Display u_7_segment_display_4 (
    .g(dec_7seg_1_g), .f(dec_7seg_1_f), .a(dec_7seg_1_a), .b(dec_7seg_1_b), .e(dec_7seg_1_e),
    .d(dec_7seg_1_d), .c(dec_7seg_1_c));  // open: dp
endmodule
