// Logisim project f6-minirv-dev.circ as structural Verilog: 2 circuits, main circuit miniRV
module miniRV (
  input  RUN,
  input  CLR,
  input  CLK
);

  wire add_out, addi_out, and_2_out, and_3_out, and_4_out, and_5_out, comparator_1_eq, comparator_2_eq,
       comparator_3_eq, comparator_4_eq, comparator_5_eq, comparator_6_eq, comparator_7_eq, comparator_8_eq,
       comparator_9_eq, decoder_1_out0, decoder_1_out1, decoder_1_out2, decoder_1_out3, jalr_out, lbu_out,
       lui_out, lw_out, or_1_out, or_2_out, or_5_out, or_6_out, or_7_out, or_8_out, or_9_out, sb_out, sw_out;
  wire [1:0] or_4_out;
  wire [4:0] rom_1_data_2;
  wire [6:0] rom_1_data_3;
  wire [7:0] gpr16x32_1_rdata2_2, multiplexer_9_out;
  wire [31:0] adder_1_out, adder_2_out, and_1_out, bit_extender_1_out, bit_extender_2_out,
       bit_extender_3_out, gpr16x32_1_rdata1, multiplexer_1_out, multiplexer_2_out, multiplexer_3_out,
       multiplexer_4_out, multiplexer_5_out, multiplexer_6_out, multiplexer_7_out, multiplexer_8_out,
       ram_1_dout, register_1_q;
  wire [31:8] gpr16x32_1_rdata2;
  wire [31:12] rom_1_data;

  or or_1 (or_1_out, RUN, CLR);
  Multiplexer #(.width(32)) multiplexer_1 (
    .in0(multiplexer_2_out), .in1({32{1'b0}}), .out(multiplexer_1_out), .sel(CLR));
  Register #(.width(32)) register_1 (.D(multiplexer_1_out), .en(or_1_out), .clk(CLK), .Q(register_1_q));  // open: clr
  // Probe on register_1_q
  Multiplexer #(.width(32)) multiplexer_2 (.in0(adder_1_out), .in1(and_1_out), .out(multiplexer_2_out), .sel(jalr_out));
  Adder #(.width(32)) adder_1 (.a(register_1_q), .b(32'h4), .out(adder_1_out));  // open: cin, cout
  // Probe on register_1_q[5:2]
  ROM #(.addrWidth(4), .dataWidth(32)) rom_1 (
    .addr(register_1_q[5:2]), .data({rom_1_data, rom_1_data_2, rom_1_data_3}));
  // Probe on {rom_1_data, rom_1_data_2, rom_1_data_3}
  assign bit_extender_1_out = {{20{rom_1_data[31]}}, rom_1_data[31:20]};  // Bit_Extender bit_extender_1
  assign bit_extender_2_out = {{20{rom_1_data[31]}}, {rom_1_data[31:25], rom_1_data_2}};  // Bit_Extender bit_extender_2
  Comparator #(.width(3)) comparator_1 (.a(3'b000), .b(rom_1_data[14:12]), .eq(comparator_1_eq));  // open: gt, lt
  Comparator #(.width(3)) comparator_2 (.a(3'b010), .b(rom_1_data[14:12]), .eq(comparator_2_eq));  // open: gt, lt
  Comparator #(.width(3)) comparator_3 (.a(3'b100), .b(rom_1_data[14:12]), .eq(comparator_3_eq));  // open: gt, lt
  Comparator #(.width(7)) comparator_4 (.a(7'b0010011), .b(rom_1_data_3), .eq(comparator_4_eq));  // open: gt, lt
  Comparator #(.width(7)) comparator_5 (.a(7'b1100111), .b(rom_1_data_3), .eq(comparator_5_eq));  // open: gt, lt
  Comparator #(.width(7)) comparator_6 (.a(7'b0110011), .b(rom_1_data_3), .eq(comparator_6_eq));  // open: gt, lt
  Comparator #(.width(7)) comparator_7 (.a(7'b0110111), .b(rom_1_data_3), .eq(comparator_7_eq));  // open: gt, lt
  Comparator #(.width(7)) comparator_8 (.a(7'b0000011), .b(rom_1_data_3), .eq(comparator_8_eq));  // open: gt, lt
  Comparator #(.width(7)) comparator_9 (.a(7'b0100011), .b(rom_1_data_3), .eq(comparator_9_eq));  // open: gt, lt
  and addi (addi_out, comparator_4_eq, comparator_1_eq);
  and jalr (jalr_out, comparator_5_eq, comparator_1_eq);
  and add (add_out, comparator_6_eq, comparator_1_eq);
  buf lui (lui_out, comparator_7_eq);  // AND_Gate
  and lw (lw_out, comparator_8_eq, comparator_2_eq);
  and sw (sw_out, comparator_9_eq, comparator_2_eq);
  and lbu (lbu_out, comparator_8_eq, comparator_3_eq);
  and sb (sb_out, comparator_9_eq, comparator_1_eq);
  Multiplexer #(.select(2), .width(32)) multiplexer_3 (
    .in0(adder_2_out), .in1(adder_1_out), .in2({rom_1_data, {12{1'b0}}}), .in3(multiplexer_7_out),
    .out(multiplexer_3_out), .sel(or_4_out));
  or or_2 (or_2_out, addi_out, jalr_out, add_out, lui_out, lw_out, lbu_out);
  or or_3 (or_4_out[1], lui_out, lw_out, lbu_out);
  or or_4 (or_4_out[0], jalr_out, lw_out, lbu_out);
  gpr16x32 gpr16x32_1 (
    .CLK(CLK), .wdata(multiplexer_3_out), .CLR(CLR), .waddr(rom_1_data_2[3:0]), .wen(or_2_out),
    .raddr1(rom_1_data[18:15]), .raddr2(rom_1_data[23:20]), .rdata1(gpr16x32_1_rdata1),
    .rdata2({gpr16x32_1_rdata2, gpr16x32_1_rdata2_2}));
  Multiplexer #(.width(32)) multiplexer_4 (
    .in0(bit_extender_1_out), .in1(bit_extender_2_out), .out(multiplexer_4_out), .sel(or_5_out));
  or or_5 (or_5_out, sw_out, sb_out);
  assign and_1_out = 32'hfffffffe & adder_2_out;  // AND_Gate and_1, 32 bits wide
  Multiplexer #(.width(32)) multiplexer_5 (
    .in0(multiplexer_4_out), .in1({gpr16x32_1_rdata2, gpr16x32_1_rdata2_2}), .out(multiplexer_5_out),
    .sel(add_out));
  Decoder #(.select(2)) decoder_1 (
    .out0(decoder_1_out0), .out1(decoder_1_out1), .out2(decoder_1_out2), .out3(decoder_1_out3),
    .sel(adder_2_out[1:0]));  // open: en
  Multiplexer #(.select(2), .width(32)) multiplexer_6 (
    .in0({{24{1'b0}}, gpr16x32_1_rdata2_2}), .in1({{16{1'b0}}, gpr16x32_1_rdata2_2, {8{1'b0}}}),
    .in2({{8{1'b0}}, gpr16x32_1_rdata2_2, {16{1'b0}}}), .in3({gpr16x32_1_rdata2_2, {24{1'b0}}}),
    .out(multiplexer_6_out), .sel(adder_2_out[1:0]));
  Multiplexer #(.width(32)) multiplexer_7 (
    .in0(ram_1_dout), .in1(bit_extender_3_out), .out(multiplexer_7_out), .sel(lbu_out));
  Adder #(.width(32)) adder_2 (.a(gpr16x32_1_rdata1), .b(multiplexer_5_out), .out(adder_2_out));  // open: cin, cout
  Multiplexer #(.width(32)) multiplexer_8 (
    .in0({gpr16x32_1_rdata2, gpr16x32_1_rdata2_2}), .in1(multiplexer_6_out), .out(multiplexer_8_out),
    .sel(sb_out));
  or or_6 (or_6_out, and_2_out, sw_out);
  and and_2 (and_2_out, decoder_1_out3, sb_out);
  or or_7 (or_7_out, and_3_out, sw_out);
  or or_8 (or_8_out, and_4_out, sw_out);
  and and_3 (and_3_out, decoder_1_out2, sb_out);
  and and_4 (and_4_out, decoder_1_out1, sb_out);
  RAM #(.addrWidth(6), .asyncread("true"), .byteenables("byteEnables"), .dataWidth(32), .\type ("nonvolatile")) ram_1 (
    .addr(adder_2_out[7:2]), .we(or_5_out), .oe(1'b1), .clk(CLK), .din(multiplexer_8_out), .dout(ram_1_dout),
    .be3(or_6_out), .be2(or_7_out), .be1(or_8_out), .be0(or_9_out));
  or or_9 (or_9_out, and_5_out, sw_out);
  and and_5 (and_5_out, decoder_1_out0, sb_out);
  Multiplexer #(.select(2), .width(8)) multiplexer_9 (
    .in0(ram_1_dout[7:0]), .in1(ram_1_dout[15:8]), .in2(ram_1_dout[23:16]), .in3(ram_1_dout[31:24]),
    .out(multiplexer_9_out), .sel(adder_2_out[1:0]));
  assign bit_extender_3_out = {{24{1'b0}}, multiplexer_9_out};  // Bit_Extender bit_extender_3

  // Notes on the sheet:
  //   contents of rom_1 (hex, n*v repeats v):
  //   402283 9000313 6003a3 ab00313 600323 cd00313 6002a3 ef00313 600223 402383 2800067
endmodule

module gpr16x32 (
  input  CLK,
  input  [31:0] wdata,
  input  CLR,
  input  [3:0] waddr,
  input  wen,
  input  [3:0] raddr1,
  input  [3:0] raddr2,
  output [31:0] rdata1,
  output [31:0] rdata2
);

  wire decoder_1_out1, decoder_1_out2, decoder_1_out3, decoder_1_out4, decoder_1_out5, decoder_1_out6,
       decoder_1_out7, decoder_1_out8, decoder_1_out9, decoder_1_out10, decoder_1_out11, decoder_1_out12,
       decoder_1_out13, decoder_1_out14, decoder_1_out15;
  wire [31:0] register_1_q, register_2_q, register_3_q, register_4_q, register_5_q, register_6_q,
       register_7_q, register_8_q, register_9_q, register_10_q, register_11_q, register_12_q, register_13_q,
       register_14_q, register_15_q, register_16_q;

  Decoder #(.select(4)) decoder_1 (
    .out1(decoder_1_out1), .out2(decoder_1_out2), .out3(decoder_1_out3), .out4(decoder_1_out4),
    .out5(decoder_1_out5), .out6(decoder_1_out6), .out7(decoder_1_out7), .out8(decoder_1_out8),
    .out9(decoder_1_out9), .out10(decoder_1_out10), .out11(decoder_1_out11), .out12(decoder_1_out12),
    .out13(decoder_1_out13), .out14(decoder_1_out14), .out15(decoder_1_out15), .sel(waddr), .en(wen));  // open: out0
  Register #(.width(32)) register_1 (.D({32{1'b0}}), .en(1'b0), .clk(CLK), .Q(register_1_q), .clr(CLR));
  Register #(.width(32)) register_2 (.D(wdata), .en(decoder_1_out8), .clk(CLK), .Q(register_2_q), .clr(CLR));
  Register #(.width(32)) register_3 (.D(wdata), .en(decoder_1_out1), .clk(CLK), .Q(register_3_q), .clr(CLR));
  Register #(.width(32)) register_4 (.D(wdata), .en(decoder_1_out9), .clk(CLK), .Q(register_4_q), .clr(CLR));
  Register #(.width(32)) register_5 (.D(wdata), .en(decoder_1_out2), .clk(CLK), .Q(register_5_q), .clr(CLR));
  Register #(.width(32)) register_6 (.D(wdata), .en(decoder_1_out10), .clk(CLK), .Q(register_6_q), .clr(CLR));
  Register #(.width(32)) register_7 (.D(wdata), .en(decoder_1_out3), .clk(CLK), .Q(register_7_q), .clr(CLR));
  Register #(.width(32)) register_8 (.D(wdata), .en(decoder_1_out11), .clk(CLK), .Q(register_8_q), .clr(CLR));
  Register #(.width(32)) register_9 (.D(wdata), .en(decoder_1_out4), .clk(CLK), .Q(register_9_q), .clr(CLR));
  Register #(.width(32)) register_10 (.D(wdata), .en(decoder_1_out12), .clk(CLK), .Q(register_10_q), .clr(CLR));
  Register #(.width(32)) register_11 (.D(wdata), .en(decoder_1_out5), .clk(CLK), .Q(register_11_q), .clr(CLR));
  Register #(.width(32)) register_12 (.D(wdata), .en(decoder_1_out13), .clk(CLK), .Q(register_12_q), .clr(CLR));
  Register #(.width(32)) register_13 (.D(wdata), .en(decoder_1_out6), .clk(CLK), .Q(register_13_q), .clr(CLR));
  Register #(.width(32)) register_14 (.D(wdata), .en(decoder_1_out14), .clk(CLK), .Q(register_14_q), .clr(CLR));
  Register #(.width(32)) register_15 (.D(wdata), .en(decoder_1_out7), .clk(CLK), .Q(register_15_q), .clr(CLR));
  Register #(.width(32)) register_16 (.D(wdata), .en(decoder_1_out15), .clk(CLK), .Q(register_16_q), .clr(CLR));
  Multiplexer #(.select(4), .width(32)) multiplexer_1 (
    .in0(register_1_q), .in1(register_3_q), .in2(register_5_q), .in3(register_7_q), .in4(register_9_q),
    .in5(register_11_q), .in6(register_13_q), .in7(register_15_q), .in8(register_2_q), .in9(register_4_q),
    .in10(register_6_q), .in11(register_8_q), .in12(register_10_q), .in13(register_12_q),
    .in14(register_14_q), .in15(register_16_q), .out(rdata1), .sel(raddr1));
  Multiplexer #(.select(4), .width(32)) multiplexer_2 (
    .in0(register_1_q), .in1(register_3_q), .in2(register_5_q), .in3(register_7_q), .in4(register_9_q),
    .in5(register_11_q), .in6(register_13_q), .in7(register_15_q), .in8(register_2_q), .in9(register_4_q),
    .in10(register_6_q), .in11(register_8_q), .in12(register_10_q), .in13(register_12_q),
    .in14(register_14_q), .in15(register_16_q), .out(rdata2), .sel(raddr2));
endmodule
